// Logisim project S2-T22 .circ as structural Verilog: 12 circuits, main circuit final
module _4_bit_binary_to_BCD_converter (
  input  I3,
  input  I2,
  input  I1,
  input  I0,
  output A3,
  output A2,
  output A1,
  output A0
);

  wire and_1_out, and_2_out, and_3_out, and_4_out, and_5_out, and_6_out, and_7_out, and_8_out, and_9_out,
       and_10_out, not_1_out, not_2_out, not_3_out, not_4_out;

  and and_1 (and_1_out, I2, I1);
  and and_2 (and_2_out, I2, I0);
  or or_1 (A3, I3, and_1_out, and_2_out);
  and and_3 (and_3_out, I0, I3);
  and and_4 (and_4_out, I2, not_3_out, not_4_out);
  or or_2 (A2, and_3_out, and_4_out);
  and and_5 (and_5_out, not_2_out, I1);
  and and_6 (and_6_out, I3, not_4_out);
  and and_7 (and_7_out, I1, I0);
  or or_3 (A1, and_5_out, and_6_out, and_7_out);
  not not_1 (not_1_out, I3);
  and and_8 (and_8_out, I3, not_4_out);
  not not_2 (not_2_out, I2);
  and and_9 (and_9_out, I2, not_4_out, I1);
  or or_4 (A0, and_8_out, and_9_out, and_10_out);
  not not_3 (not_3_out, I1);
  not not_4 (not_4_out, I0);
  and and_10 (and_10_out, not_1_out, not_2_out, I0);

  // Notes on the sheet:
  //   Output
  //   Input
endmodule

module _7_bit_binary_to_BCD_converter (
  input  [6:0] _7_bit_binary_input,
  output [3:0] Output_LSB,
  output [3:0] Output_MSB
);

  wire bitselector_1_out, bitselector_2_out, bitselector_3_out, bitselector_4_out, bitselector_5_out,
       bitselector_6_out, bitselector_7_out, n4_bit_binary_to_bcd_converter_1_a0,
       n4_bit_binary_to_bcd_converter_1_a1, n4_bit_binary_to_bcd_converter_1_a2,
       n4_bit_binary_to_bcd_converter_2_a0, n4_bit_binary_to_bcd_converter_2_a1,
       n4_bit_binary_to_bcd_converter_2_a2, n4_bit_binary_to_bcd_converter_2_a3,
       n4_bit_binary_to_bcd_converter_3_a0, n4_bit_binary_to_bcd_converter_3_a1,
       n4_bit_binary_to_bcd_converter_3_a2, n4_bit_binary_to_bcd_converter_3_a3,
       n4_bit_binary_to_bcd_converter_4_a0, n4_bit_binary_to_bcd_converter_4_a1,
       n4_bit_binary_to_bcd_converter_4_a2, n4_bit_binary_to_bcd_converter_4_a3,
       n4_bit_binary_to_bcd_converter_5_a0, n4_bit_binary_to_bcd_converter_5_a1,
       n4_bit_binary_to_bcd_converter_5_a2, n4_bit_binary_to_bcd_converter_6_a0,
       n4_bit_binary_to_bcd_converter_6_a1, n4_bit_binary_to_bcd_converter_6_a2,
       n4_bit_binary_to_bcd_converter_6_a3, n4_bit_binary_to_bcd_converter_7_a0,
       n4_bit_binary_to_bcd_converter_7_a1, n4_bit_binary_to_bcd_converter_7_a2,
       n4_bit_binary_to_bcd_converter_7_a3;
  wire [3:0] adder_1_out, adder_2_out, adder_3_out, adder_4_out, bit_extender_1_out, bit_extender_2_out,
       bit_extender_3_out, bit_extender_4_out, bit_extender_5_out, bit_extender_6_out, bit_extender_7_out,
       bit_extender_8_out, shifter_1_out, shifter_2_out, shifter_3_out, shifter_4_out, shifter_5_out,
       shifter_6_out;

  BitSelector #(.width(7)) bitselector_1 (.in(_7_bit_binary_input), .out(bitselector_1_out), .sel(3'b110));
  BitSelector #(.width(7)) bitselector_2 (.in(_7_bit_binary_input), .out(bitselector_2_out), .sel(3'b101));
  BitSelector #(.width(7)) bitselector_3 (.in(_7_bit_binary_input), .out(bitselector_3_out), .sel(3'b100));
  BitSelector #(.width(7)) bitselector_4 (.in(_7_bit_binary_input), .out(bitselector_4_out), .sel(3'b011));
  BitSelector #(.width(7)) bitselector_5 (.in(_7_bit_binary_input), .out(bitselector_5_out), .sel(3'b010));
  BitSelector #(.width(7)) bitselector_6 (.in(_7_bit_binary_input), .out(bitselector_6_out), .sel(3'b001));
  BitSelector #(.width(7)) bitselector_7 (.in(_7_bit_binary_input), .out(bitselector_7_out), .sel(3'b000));
  _4_bit_binary_to_BCD_converter u_4_bit_binary_to_bcd_converter_1 (
    .I3(1'b0), .I2(n4_bit_binary_to_bcd_converter_2_a3), .I1(n4_bit_binary_to_bcd_converter_3_a3),
    .I0(n4_bit_binary_to_bcd_converter_4_a3), .A2(n4_bit_binary_to_bcd_converter_1_a2),
    .A1(n4_bit_binary_to_bcd_converter_1_a1), .A0(n4_bit_binary_to_bcd_converter_1_a0));  // open: A3
  _4_bit_binary_to_BCD_converter u_4_bit_binary_to_bcd_converter_2 (
    .I3(1'b0), .I2(1'b0), .I1(bitselector_1_out), .I0(bitselector_2_out),
    .A3(n4_bit_binary_to_bcd_converter_2_a3), .A2(n4_bit_binary_to_bcd_converter_2_a2),
    .A1(n4_bit_binary_to_bcd_converter_2_a1), .A0(n4_bit_binary_to_bcd_converter_2_a0));
  _4_bit_binary_to_BCD_converter u_4_bit_binary_to_bcd_converter_3 (
    .I3(n4_bit_binary_to_bcd_converter_2_a2), .I2(n4_bit_binary_to_bcd_converter_2_a1),
    .I1(n4_bit_binary_to_bcd_converter_2_a0), .I0(bitselector_3_out),
    .A3(n4_bit_binary_to_bcd_converter_3_a3), .A2(n4_bit_binary_to_bcd_converter_3_a2),
    .A1(n4_bit_binary_to_bcd_converter_3_a1), .A0(n4_bit_binary_to_bcd_converter_3_a0));
  _4_bit_binary_to_BCD_converter u_4_bit_binary_to_bcd_converter_4 (
    .I3(n4_bit_binary_to_bcd_converter_3_a2), .I2(n4_bit_binary_to_bcd_converter_3_a1),
    .I1(n4_bit_binary_to_bcd_converter_3_a0), .I0(bitselector_4_out),
    .A3(n4_bit_binary_to_bcd_converter_4_a3), .A2(n4_bit_binary_to_bcd_converter_4_a2),
    .A1(n4_bit_binary_to_bcd_converter_4_a1), .A0(n4_bit_binary_to_bcd_converter_4_a0));
  _4_bit_binary_to_BCD_converter u_4_bit_binary_to_bcd_converter_5 (
    .I3(n4_bit_binary_to_bcd_converter_1_a2), .I2(n4_bit_binary_to_bcd_converter_1_a1),
    .I1(n4_bit_binary_to_bcd_converter_1_a0), .I0(n4_bit_binary_to_bcd_converter_6_a3),
    .A2(n4_bit_binary_to_bcd_converter_5_a2), .A1(n4_bit_binary_to_bcd_converter_5_a1),
    .A0(n4_bit_binary_to_bcd_converter_5_a0));  // open: A3
  _4_bit_binary_to_BCD_converter u_4_bit_binary_to_bcd_converter_6 (
    .I3(n4_bit_binary_to_bcd_converter_4_a2), .I2(n4_bit_binary_to_bcd_converter_4_a1),
    .I1(n4_bit_binary_to_bcd_converter_4_a0), .I0(bitselector_5_out),
    .A3(n4_bit_binary_to_bcd_converter_6_a3), .A2(n4_bit_binary_to_bcd_converter_6_a2),
    .A1(n4_bit_binary_to_bcd_converter_6_a1), .A0(n4_bit_binary_to_bcd_converter_6_a0));
  _4_bit_binary_to_BCD_converter u_4_bit_binary_to_bcd_converter_7 (
    .I3(n4_bit_binary_to_bcd_converter_6_a2), .I2(n4_bit_binary_to_bcd_converter_6_a1),
    .I1(n4_bit_binary_to_bcd_converter_6_a0), .I0(bitselector_6_out),
    .A3(n4_bit_binary_to_bcd_converter_7_a3), .A2(n4_bit_binary_to_bcd_converter_7_a2),
    .A1(n4_bit_binary_to_bcd_converter_7_a1), .A0(n4_bit_binary_to_bcd_converter_7_a0));
  assign bit_extender_1_out = {{3{1'b0}}, bitselector_7_out};  // Bit_Extender bit_extender_1
  assign bit_extender_2_out = {{3{1'b0}}, n4_bit_binary_to_bcd_converter_7_a0};  // Bit_Extender bit_extender_2
  assign bit_extender_3_out = {{3{1'b0}}, n4_bit_binary_to_bcd_converter_7_a1};  // Bit_Extender bit_extender_3
  assign bit_extender_4_out = {{3{1'b0}}, n4_bit_binary_to_bcd_converter_7_a2};  // Bit_Extender bit_extender_4
  assign bit_extender_5_out = {{3{1'b0}}, n4_bit_binary_to_bcd_converter_7_a3};  // Bit_Extender bit_extender_5
  assign bit_extender_6_out = {{3{1'b0}}, n4_bit_binary_to_bcd_converter_5_a0};  // Bit_Extender bit_extender_6
  assign bit_extender_7_out = {{3{1'b0}}, n4_bit_binary_to_bcd_converter_5_a1};  // Bit_Extender bit_extender_7
  assign bit_extender_8_out = {{3{1'b0}}, n4_bit_binary_to_bcd_converter_5_a2};  // Bit_Extender bit_extender_8
  Shifter #(.width(4)) shifter_1 (.in(bit_extender_2_out), .\dist (2'b01), .out(shifter_1_out));
  Shifter #(.width(4)) shifter_2 (.in(bit_extender_3_out), .\dist (2'b10), .out(shifter_2_out));
  Shifter #(.width(4)) shifter_3 (.in(bit_extender_4_out), .\dist (2'b11), .out(shifter_3_out));
  Shifter #(.width(4)) shifter_4 (.in(bit_extender_6_out), .\dist (2'b01), .out(shifter_4_out));
  Shifter #(.width(4)) shifter_5 (.in(bit_extender_7_out), .\dist (2'b10), .out(shifter_5_out));
  Shifter #(.width(4)) shifter_6 (.in(bit_extender_8_out), .\dist (2'b11), .out(shifter_6_out));
  Adder #(.width(4)) adder_1 (.a(bit_extender_1_out), .b(shifter_1_out), .out(adder_1_out));  // open: cin, cout
  Adder #(.width(4)) adder_2 (.a(shifter_2_out), .b(shifter_3_out), .out(adder_2_out));  // open: cin, cout
  Adder #(.width(4)) adder_3 (.a(bit_extender_5_out), .b(shifter_4_out), .out(adder_3_out));  // open: cin, cout
  Adder #(.width(4)) adder_4 (.a(shifter_5_out), .b(shifter_6_out), .out(adder_4_out));  // open: cin, cout
  Adder #(.width(4)) adder_5 (.a(adder_1_out), .b(adder_2_out), .out(Output_LSB));  // open: cin, cout
  Adder #(.width(4)) adder_6 (.a(adder_3_out), .b(adder_4_out), .out(Output_MSB));  // open: cin, cout

  // Notes on the sheet:
  //   4 bit binary to BCD converter
  //   4 bit binary to BCD converter
  //   4 bit binary to BCD converter
  //   4 bit binary to BCD converter
  //   4 bit bin ary to BCD converter
endmodule

module Bill_calculator_module_for_pwd_special_room (
  input  [2:0] Number_of_days,
  input  AC_selection,
  input  Wi_Fi_selection,
  output [3:0] LSB,
  output [3:0] out_5,
  output [3:0] out_6,
  output [3:0] out_7,
  output [3:0] MSB
);

  wire adder_1_cout, adder_2_cout, adder_3_cout, adder_4_cout, adder_5_cout, adder_6_cout, adder_7_cout,
       adder_8_cout, adder_9_cout, adder_10_cout, adder_11_cout, adder_12_cout, adder_13_cout, adder_14_cout,
       adder_20_cout, adder_21_cout, adder_22_cout, adder_23_cout, adder_24_cout, adder_25_cout,
       adder_26_cout, adder_27_cout, adder_28_cout, comparator_1_gt, comparator_2_gt, comparator_3_gt,
       comparator_4_gt, comparator_5_gt, comparator_6_gt, comparator_7_gt, comparator_8_gt, comparator_9_gt,
       comparator_10_gt, comparator_11_gt, comparator_12_gt, or_1_out, or_2_out, or_3_out, or_4_out,
       or_5_out, or_6_out, or_7_out, or_8_out, or_9_out, or_10_out, or_11_out, or_12_out, or_13_out,
       or_14_out, or_15_out, or_16_out, or_17_out, or_18_out, or_19_out, or_20_out, or_21_out, or_22_out;
  wire [3:0] adder_1_out, adder_2_out, adder_3_out, adder_4_out, adder_5_out, adder_6_out, adder_7_out,
       adder_8_out, adder_9_out, adder_10_out, adder_11_out, adder_12_out, adder_13_out, adder_14_out,
       adder_20_out, adder_21_out, adder_22_out, adder_23_out, adder_24_out, bit_extender_1_out,
       bit_extender_2_out, bit_extender_3_out, multiplexer_1_out, multiplexer_2_out, multiplexer_3_out,
       multiplexer_4_out, multiplexer_5_out, multiplexer_6_out, multiplexer_7_out, multiplexer_8_out,
       multiplexer_9_out, multiplexer_10_out, multiplexer_11_out, multiplexer_12_out, multiplexer_13_out,
       multiplexer_14_out, multiplexer_15_out, multiplexer_16_out, multiplexer_17_out, multiplexer_18_out,
       multiplier_1_cout, multiplier_1_out, multiplier_2_cout, multiplier_2_out, multiplier_3_cout,
       multiplier_3_out, multiplier_4_cout, multiplier_4_out, multiplier_5_cout, multiplier_5_out,
       n7_bit_binary_to_bcd_converter_1_output_lsb, n7_bit_binary_to_bcd_converter_1_output_msb,
       n7_bit_binary_to_bcd_converter_2_output_lsb, n7_bit_binary_to_bcd_converter_2_output_msb,
       n7_bit_binary_to_bcd_converter_3_output_lsb, n7_bit_binary_to_bcd_converter_3_output_msb,
       n7_bit_binary_to_bcd_converter_4_output_lsb, n7_bit_binary_to_bcd_converter_4_output_msb,
       n7_bit_binary_to_bcd_converter_5_output_lsb;
  wire [6:0] adder_15_out, adder_16_out, adder_17_out, adder_18_out, adder_19_out, bit_extender_4_out,
       bit_extender_5_out, bit_extender_6_out, bit_extender_7_out, bit_extender_8_out, bit_extender_9_out,
       bit_extender_10_out, bit_extender_11_out, bit_extender_12_out, bit_extender_13_out, shifter_1_out,
       shifter_2_out, shifter_3_out, shifter_4_out, shifter_5_out;

  Multiplexer #(.width(4), .enable("false")) multiplexer_1 (
    .in0(4'b0000), .in1(4'b0000), .out(multiplexer_1_out), .sel(AC_selection));
  Multiplexer #(.width(4), .enable("false")) multiplexer_2 (
    .in0(4'b0000), .in1(4'b0000), .out(multiplexer_2_out), .sel(AC_selection));
  Multiplexer #(.width(4), .enable("false")) multiplexer_3 (
    .in0(4'b0000), .in1(4'b0010), .out(multiplexer_3_out), .sel(AC_selection));
  Multiplexer #(.width(4), .enable("false")) multiplexer_4 (
    .in0(4'b0000), .in1(4'b0000), .out(multiplexer_4_out), .sel(Wi_Fi_selection));
  Multiplexer #(.width(4), .enable("false")) multiplexer_5 (
    .in0(4'b0000), .in1(4'b0000), .out(multiplexer_5_out), .sel(Wi_Fi_selection));
  Multiplexer #(.width(4), .enable("false")) multiplexer_6 (
    .in0(4'b0000), .in1(4'b0001), .out(multiplexer_6_out), .sel(Wi_Fi_selection));
  or or_1 (or_1_out, adder_1_cout, adder_4_cout);
  or or_2 (or_2_out, adder_2_cout, adder_5_cout);
  Adder #(.width(4)) adder_1 (
    .a(multiplexer_4_out), .b(multiplexer_1_out), .out(adder_1_out), .cout(adder_1_cout));  // open: cin
  Adder #(.width(4)) adder_2 (
    .a(multiplexer_5_out), .b(multiplexer_2_out), .out(adder_2_out), .cin(or_1_out), .cout(adder_2_cout));
  Adder #(.width(4)) adder_3 (
    .a(multiplexer_6_out), .b(multiplexer_3_out), .out(adder_3_out), .cin(or_2_out), .cout(adder_3_cout));
  or or_3 (or_3_out, adder_3_cout, adder_6_cout);
  Comparator #(.width(4), .mode("unsigned")) comparator_1 (
    .a(adder_1_out), .b(4'b1001), .gt(comparator_1_gt));  // open: eq, lt
  Comparator #(.width(4), .mode("unsigned")) comparator_2 (
    .a(adder_2_out), .b(4'b1001), .gt(comparator_2_gt));  // open: eq, lt
  Comparator #(.width(4), .mode("unsigned")) comparator_3 (
    .a(adder_3_out), .b(4'b1001), .gt(comparator_3_gt));  // open: eq, lt
  or or_4 (or_4_out, comparator_1_gt, adder_1_cout);
  or or_5 (or_5_out, comparator_2_gt, adder_2_cout);
  or or_6 (or_6_out, comparator_3_gt, adder_3_cout);
  Multiplexer #(.width(4), .enable("false")) multiplexer_7 (
    .in0(4'b0000), .in1(4'b0110), .out(multiplexer_7_out), .sel(or_4_out));
  Multiplexer #(.width(4), .enable("false")) multiplexer_8 (
    .in0(4'b0000), .in1(4'b0110), .out(multiplexer_8_out), .sel(or_5_out));
  Multiplexer #(.width(4), .enable("false")) multiplexer_9 (
    .in0(4'b0000), .in1(4'b0110), .out(multiplexer_9_out), .sel(or_6_out));
  Adder #(.width(4)) adder_4 (
    .a(adder_1_out), .b(multiplexer_7_out), .out(adder_4_out), .cout(adder_4_cout));  // open: cin
  Adder #(.width(4)) adder_5 (
    .a(adder_2_out), .b(multiplexer_8_out), .out(adder_5_out), .cout(adder_5_cout));  // open: cin
  Adder #(.width(4)) adder_6 (
    .a(adder_3_out), .b(multiplexer_9_out), .out(adder_6_out), .cout(adder_6_cout));  // open: cin
  assign bit_extender_1_out = {{3{1'b0}}, or_3_out};  // Bit_Extender bit_extender_1
  Adder #(.width(4)) adder_7 (.a(4'b0000), .b(adder_4_out), .out(adder_7_out), .cout(adder_7_cout));  // open: cin
  or or_7 (or_7_out, adder_7_cout, adder_11_cout);
  Adder #(.width(4)) adder_8 (.a(4'b0000), .b(adder_5_out), .out(adder_8_out), .cin(or_7_out), .cout(adder_8_cout));
  or or_8 (or_8_out, adder_8_cout, adder_12_cout);
  Adder #(.width(4)) adder_9 (.a(4'b0101), .b(adder_6_out), .out(adder_9_out), .cin(or_8_out), .cout(adder_9_cout));
  or or_9 (or_9_out, adder_9_cout, adder_13_cout);
  Adder #(.width(4)) adder_10 (
    .a(4'b0000), .b(bit_extender_1_out), .out(adder_10_out), .cin(or_9_out), .cout(adder_10_cout));
  Comparator #(.width(4), .mode("unsigned")) comparator_4 (
    .a(adder_7_out), .b(4'b1001), .gt(comparator_4_gt));  // open: eq, lt
  Comparator #(.width(4), .mode("unsigned")) comparator_5 (
    .a(adder_8_out), .b(4'b1001), .gt(comparator_5_gt));  // open: eq, lt
  Comparator #(.width(4), .mode("unsigned")) comparator_6 (
    .a(adder_9_out), .b(4'b1001), .gt(comparator_6_gt));  // open: eq, lt
  Comparator #(.width(4), .mode("unsigned")) comparator_7 (
    .a(adder_10_out), .b(4'b1001), .gt(comparator_7_gt));  // open: eq, lt
  or or_10 (or_10_out, comparator_4_gt, adder_7_cout);
  or or_11 (or_11_out, comparator_5_gt, adder_8_cout);
  or or_12 (or_12_out, comparator_6_gt, adder_9_cout);
  or or_13 (or_13_out, comparator_7_gt, adder_10_cout);
  Multiplexer #(.width(4), .enable("false")) multiplexer_10 (
    .in0(4'b0000), .in1(4'b0110), .out(multiplexer_10_out), .sel(or_10_out));
  Multiplexer #(.width(4), .enable("false")) multiplexer_11 (
    .in0(4'b0000), .in1(4'b0110), .out(multiplexer_11_out), .sel(or_11_out));
  Multiplexer #(.width(4), .enable("false")) multiplexer_12 (
    .in0(4'b0000), .in1(4'b0110), .out(multiplexer_12_out), .sel(or_12_out));
  Multiplexer #(.width(4), .enable("false")) multiplexer_13 (
    .in0(4'b0000), .in1(4'b0110), .out(multiplexer_13_out), .sel(or_13_out));
  Adder #(.width(4)) adder_11 (
    .a(adder_7_out), .b(multiplexer_10_out), .out(adder_11_out), .cout(adder_11_cout));  // open: cin
  Adder #(.width(4)) adder_12 (
    .a(adder_8_out), .b(multiplexer_11_out), .out(adder_12_out), .cout(adder_12_cout));  // open: cin
  Adder #(.width(4)) adder_13 (
    .a(adder_9_out), .b(multiplexer_12_out), .out(adder_13_out), .cout(adder_13_cout));  // open: cin
  Adder #(.width(4)) adder_14 (
    .a(adder_10_out), .b(multiplexer_13_out), .out(adder_14_out), .cout(adder_14_cout));  // open: cin
  assign bit_extender_2_out = {{1{1'b0}}, Number_of_days};  // Bit_Extender bit_extender_2
  assign bit_extender_3_out = {{3{1'b0}}, adder_14_cout};  // Bit_Extender bit_extender_3
  Multiplier #(.width(4)) multiplier_1 (
    .a(adder_11_out), .b(bit_extender_2_out), .out(multiplier_1_out), .cout(multiplier_1_cout));  // open: cin
  Multiplier #(.width(4)) multiplier_2 (
    .a(bit_extender_2_out), .b(adder_12_out), .out(multiplier_2_out), .cout(multiplier_2_cout));  // open: cin
  Multiplier #(.width(4)) multiplier_3 (
    .a(bit_extender_2_out), .b(adder_13_out), .out(multiplier_3_out), .cout(multiplier_3_cout));  // open: cin
  Multiplier #(.width(4)) multiplier_4 (
    .a(bit_extender_2_out), .b(adder_14_out), .out(multiplier_4_out), .cout(multiplier_4_cout));  // open: cin
  Multiplier #(.width(4)) multiplier_5 (
    .a(bit_extender_2_out), .b(bit_extender_3_out), .out(multiplier_5_out), .cout(multiplier_5_cout));  // open: cin
  assign bit_extender_4_out = {{3{1'b0}}, multiplier_1_out};  // Bit_Extender bit_extender_4
  assign bit_extender_5_out = {{3{1'b0}}, multiplier_1_cout};  // Bit_Extender bit_extender_5
  assign bit_extender_6_out = {{3{1'b0}}, multiplier_2_out};  // Bit_Extender bit_extender_6
  assign bit_extender_7_out = {{3{1'b0}}, multiplier_2_cout};  // Bit_Extender bit_extender_7
  assign bit_extender_8_out = {{3{1'b0}}, multiplier_3_out};  // Bit_Extender bit_extender_8
  assign bit_extender_9_out = {{3{1'b0}}, multiplier_3_cout};  // Bit_Extender bit_extender_9
  assign bit_extender_10_out = {{3{1'b0}}, multiplier_4_out};  // Bit_Extender bit_extender_10
  assign bit_extender_11_out = {{3{1'b0}}, multiplier_4_cout};  // Bit_Extender bit_extender_11
  assign bit_extender_12_out = {{3{1'b0}}, multiplier_5_out};  // Bit_Extender bit_extender_12
  assign bit_extender_13_out = {{3{1'b0}}, multiplier_5_cout};  // Bit_Extender bit_extender_13
  Shifter #(.width(7)) shifter_1 (.in(bit_extender_5_out), .\dist (3'b100), .out(shifter_1_out));
  Shifter #(.width(7)) shifter_2 (.in(bit_extender_7_out), .\dist (3'b100), .out(shifter_2_out));
  Shifter #(.width(7)) shifter_3 (.in(bit_extender_9_out), .\dist (3'b100), .out(shifter_3_out));
  Shifter #(.width(7)) shifter_4 (.in(bit_extender_11_out), .\dist (3'b100), .out(shifter_4_out));
  Shifter #(.width(7)) shifter_5 (.in(bit_extender_13_out), .\dist (3'b100), .out(shifter_5_out));
  Adder #(.width(7)) adder_15 (.a(bit_extender_4_out), .b(shifter_1_out), .out(adder_15_out));  // open: cin, cout
  Adder #(.width(7)) adder_16 (.a(bit_extender_6_out), .b(shifter_2_out), .out(adder_16_out));  // open: cin, cout
  Adder #(.width(7)) adder_17 (.a(bit_extender_8_out), .b(shifter_3_out), .out(adder_17_out));  // open: cin, cout
  Adder #(.width(7)) adder_18 (.a(bit_extender_10_out), .b(shifter_4_out), .out(adder_18_out));  // open: cin, cout
  Adder #(.width(7)) adder_19 (.a(bit_extender_12_out), .b(shifter_5_out), .out(adder_19_out));  // open: cin, cout
  _7_bit_binary_to_BCD_converter u_7_bit_binary_to_bcd_converter_1 (
    .Output_LSB(n7_bit_binary_to_bcd_converter_1_output_lsb),
    .Output_MSB(n7_bit_binary_to_bcd_converter_1_output_msb), ._7_bit_binary_input(adder_15_out));
  _7_bit_binary_to_BCD_converter u_7_bit_binary_to_bcd_converter_2 (
    .Output_LSB(n7_bit_binary_to_bcd_converter_2_output_lsb),
    .Output_MSB(n7_bit_binary_to_bcd_converter_2_output_msb), ._7_bit_binary_input(adder_16_out));
  _7_bit_binary_to_BCD_converter u_7_bit_binary_to_bcd_converter_3 (
    .Output_LSB(n7_bit_binary_to_bcd_converter_3_output_lsb),
    .Output_MSB(n7_bit_binary_to_bcd_converter_3_output_msb), ._7_bit_binary_input(adder_17_out));
  _7_bit_binary_to_BCD_converter u_7_bit_binary_to_bcd_converter_4 (
    .Output_LSB(n7_bit_binary_to_bcd_converter_4_output_lsb),
    .Output_MSB(n7_bit_binary_to_bcd_converter_4_output_msb), ._7_bit_binary_input(adder_18_out));
  _7_bit_binary_to_BCD_converter u_7_bit_binary_to_bcd_converter_5 (
    .Output_LSB(n7_bit_binary_to_bcd_converter_5_output_lsb), ._7_bit_binary_input(adder_19_out));  // open: Output_MSB
  or or_14 (or_14_out, adder_20_cout, adder_25_cout);
  or or_15 (or_15_out, adder_21_cout, adder_26_cout);
  or or_16 (or_16_out, adder_22_cout, adder_27_cout);
  or or_17 (or_17_out, adder_23_cout, adder_28_cout);
  Adder #(.width(4)) adder_20 (
    .a(n7_bit_binary_to_bcd_converter_1_output_lsb), .b(4'b0000), .out(adder_20_out), .cout(adder_20_cout));  // open: cin
  Adder #(.width(4)) adder_21 (
    .a(n7_bit_binary_to_bcd_converter_1_output_msb), .b(n7_bit_binary_to_bcd_converter_2_output_lsb),
    .out(adder_21_out), .cin(or_14_out), .cout(adder_21_cout));
  Adder #(.width(4)) adder_22 (
    .a(n7_bit_binary_to_bcd_converter_2_output_msb), .b(n7_bit_binary_to_bcd_converter_3_output_lsb),
    .out(adder_22_out), .cin(or_15_out), .cout(adder_22_cout));
  Adder #(.width(4)) adder_23 (
    .a(n7_bit_binary_to_bcd_converter_3_output_msb), .b(n7_bit_binary_to_bcd_converter_4_output_lsb),
    .out(adder_23_out), .cin(or_16_out), .cout(adder_23_cout));
  Adder #(.width(4)) adder_24 (
    .a(n7_bit_binary_to_bcd_converter_4_output_msb), .b(n7_bit_binary_to_bcd_converter_5_output_lsb),
    .out(adder_24_out), .cin(or_17_out), .cout(adder_24_cout));
  Comparator #(.width(4), .mode("unsigned")) comparator_8 (
    .a(adder_20_out), .b(4'b1001), .gt(comparator_8_gt));  // open: eq, lt
  Comparator #(.width(4), .mode("unsigned")) comparator_9 (
    .a(adder_21_out), .b(4'b1001), .gt(comparator_9_gt));  // open: eq, lt
  Comparator #(.width(4), .mode("unsigned")) comparator_10 (
    .a(adder_22_out), .b(4'b1001), .gt(comparator_10_gt));  // open: eq, lt
  Comparator #(.width(4), .mode("unsigned")) comparator_11 (
    .a(adder_23_out), .b(4'b1001), .gt(comparator_11_gt));  // open: eq, lt
  Comparator #(.width(4), .mode("unsigned")) comparator_12 (
    .a(adder_24_out), .b(4'b1001), .gt(comparator_12_gt));  // open: eq, lt
  or or_18 (or_18_out, comparator_8_gt, adder_20_cout);
  or or_19 (or_19_out, comparator_9_gt, adder_21_cout);
  or or_20 (or_20_out, comparator_10_gt, adder_22_cout);
  or or_21 (or_21_out, comparator_11_gt, adder_23_cout);
  Multiplexer #(.width(4), .enable("false")) multiplexer_14 (
    .in0(4'b0000), .in1(4'b0110), .out(multiplexer_14_out), .sel(or_18_out));
  Multiplexer #(.width(4), .enable("false")) multiplexer_15 (
    .in0(4'b0000), .in1(4'b0110), .out(multiplexer_15_out), .sel(or_19_out));
  Multiplexer #(.width(4), .enable("false")) multiplexer_16 (
    .in0(4'b0000), .in1(4'b0110), .out(multiplexer_16_out), .sel(or_20_out));
  Multiplexer #(.width(4), .enable("false")) multiplexer_17 (
    .in0(4'b0000), .in1(4'b0110), .out(multiplexer_17_out), .sel(or_21_out));
  Multiplexer #(.width(4), .enable("false")) multiplexer_18 (
    .in0(4'b0000), .in1(4'b0110), .out(multiplexer_18_out), .sel(or_22_out));
  or or_22 (or_22_out, comparator_12_gt, adder_24_cout);
  Adder #(.width(4)) adder_25 (.a(adder_20_out), .b(multiplexer_14_out), .out(LSB), .cout(adder_25_cout));  // open: cin
  Adder #(.width(4)) adder_26 (
    .a(adder_21_out), .b(multiplexer_15_out), .out(out_5), .cout(adder_26_cout));  // open: cin
  Adder #(.width(4)) adder_27 (
    .a(adder_22_out), .b(multiplexer_16_out), .out(out_6), .cout(adder_27_cout));  // open: cin
  Adder #(.width(4)) adder_28 (
    .a(adder_23_out), .b(multiplexer_17_out), .out(out_7), .cout(adder_28_cout));  // open: cin
  Adder #(.width(4)) adder_29 (.a(adder_24_out), .b(multiplexer_18_out), .out(MSB));  // open: cin, cout

  // Notes on the sheet:
  //   AC charges
  //   LSB
  //   MSB
  //   Wi-Fi charges
  //   LSB
  //   MSB
  //   AC+Wi-Fi charges adder 
  //   Room charges
  //   LSB
  //   MSB
  //   AC+Wi-Fi+room charges adder
  //   Multiply one day charges and number of days
  //   7 bit binary to BCD converter
  //   7 bit binary to BCD converter
  //   7 bit binary to BCD converter
  //   7 bit binary to BCD converter
  //   7 bit binary to BCD converter
  //   Convert into BCD
  //   Total bill
endmodule

module Bill_calculator_module_for_vip_room (
  input  [2:0] Number_of_days,
  input  AC_selection,
  input  Wi_Fi_selection,
  output [3:0] LSB,
  output [3:0] out_5,
  output [3:0] out_6,
  output [3:0] out_7,
  output [3:0] MSB
);

  wire adder_1_cout, adder_2_cout, adder_3_cout, adder_4_cout, adder_5_cout, adder_6_cout, adder_7_cout,
       adder_8_cout, adder_9_cout, adder_10_cout, adder_11_cout, adder_12_cout, adder_13_cout, adder_14_cout,
       adder_20_cout, adder_21_cout, adder_22_cout, adder_23_cout, adder_24_cout, adder_25_cout,
       adder_26_cout, adder_27_cout, adder_28_cout, comparator_1_gt, comparator_2_gt, comparator_3_gt,
       comparator_4_gt, comparator_5_gt, comparator_6_gt, comparator_7_gt, comparator_8_gt, comparator_9_gt,
       comparator_10_gt, comparator_11_gt, comparator_12_gt, or_1_out, or_2_out, or_3_out, or_4_out,
       or_5_out, or_6_out, or_7_out, or_8_out, or_9_out, or_10_out, or_11_out, or_12_out, or_13_out,
       or_14_out, or_15_out, or_16_out, or_17_out, or_18_out, or_19_out, or_20_out, or_21_out, or_22_out;
  wire [3:0] adder_1_out, adder_2_out, adder_3_out, adder_4_out, adder_5_out, adder_6_out, adder_7_out,
       adder_8_out, adder_9_out, adder_10_out, adder_11_out, adder_12_out, adder_13_out, adder_14_out,
       adder_20_out, adder_21_out, adder_22_out, adder_23_out, adder_24_out, bit_extender_1_out,
       bit_extender_2_out, bit_extender_3_out, multiplexer_1_out, multiplexer_2_out, multiplexer_3_out,
       multiplexer_4_out, multiplexer_5_out, multiplexer_6_out, multiplexer_7_out, multiplexer_8_out,
       multiplexer_9_out, multiplexer_10_out, multiplexer_11_out, multiplexer_12_out, multiplexer_13_out,
       multiplexer_14_out, multiplexer_15_out, multiplexer_16_out, multiplexer_17_out, multiplexer_18_out,
       multiplier_1_cout, multiplier_1_out, multiplier_2_cout, multiplier_2_out, multiplier_3_cout,
       multiplier_3_out, multiplier_4_cout, multiplier_4_out, multiplier_5_cout, multiplier_5_out,
       n7_bit_binary_to_bcd_converter_1_output_lsb, n7_bit_binary_to_bcd_converter_1_output_msb,
       n7_bit_binary_to_bcd_converter_2_output_lsb, n7_bit_binary_to_bcd_converter_2_output_msb,
       n7_bit_binary_to_bcd_converter_3_output_lsb, n7_bit_binary_to_bcd_converter_3_output_msb,
       n7_bit_binary_to_bcd_converter_4_output_lsb, n7_bit_binary_to_bcd_converter_4_output_msb,
       n7_bit_binary_to_bcd_converter_5_output_lsb;
  wire [6:0] adder_15_out, adder_16_out, adder_17_out, adder_18_out, adder_19_out, bit_extender_4_out,
       bit_extender_5_out, bit_extender_6_out, bit_extender_7_out, bit_extender_8_out, bit_extender_9_out,
       bit_extender_10_out, bit_extender_11_out, bit_extender_12_out, bit_extender_13_out, shifter_1_out,
       shifter_2_out, shifter_3_out, shifter_4_out, shifter_5_out;

  Multiplexer #(.width(4), .enable("false")) multiplexer_1 (
    .in0(4'b0000), .in1(4'b0000), .out(multiplexer_1_out), .sel(AC_selection));
  Multiplexer #(.width(4), .enable("false")) multiplexer_2 (
    .in0(4'b0000), .in1(4'b0000), .out(multiplexer_2_out), .sel(AC_selection));
  Multiplexer #(.width(4), .enable("false")) multiplexer_3 (
    .in0(4'b0000), .in1(4'b0010), .out(multiplexer_3_out), .sel(AC_selection));
  Multiplexer #(.width(4), .enable("false")) multiplexer_4 (
    .in0(4'b0000), .in1(4'b0000), .out(multiplexer_4_out), .sel(Wi_Fi_selection));
  Multiplexer #(.width(4), .enable("false")) multiplexer_5 (
    .in0(4'b0000), .in1(4'b0000), .out(multiplexer_5_out), .sel(Wi_Fi_selection));
  Multiplexer #(.width(4), .enable("false")) multiplexer_6 (
    .in0(4'b0000), .in1(4'b0001), .out(multiplexer_6_out), .sel(Wi_Fi_selection));
  Adder #(.width(4)) adder_1 (
    .a(multiplexer_4_out), .b(multiplexer_1_out), .out(adder_1_out), .cout(adder_1_cout));  // open: cin
  or or_1 (or_1_out, adder_1_cout, adder_4_cout);
  Adder #(.width(4)) adder_2 (
    .a(multiplexer_5_out), .b(multiplexer_2_out), .out(adder_2_out), .cin(or_1_out), .cout(adder_2_cout));
  or or_2 (or_2_out, adder_2_cout, adder_5_cout);
  Adder #(.width(4)) adder_3 (
    .a(multiplexer_6_out), .b(multiplexer_3_out), .out(adder_3_out), .cin(or_2_out), .cout(adder_3_cout));
  or or_3 (or_3_out, adder_3_cout, adder_6_cout);
  Comparator #(.width(4), .mode("unsigned")) comparator_1 (
    .a(adder_1_out), .b(4'b1001), .gt(comparator_1_gt));  // open: eq, lt
  Comparator #(.width(4), .mode("unsigned")) comparator_2 (
    .a(adder_2_out), .b(4'b1001), .gt(comparator_2_gt));  // open: eq, lt
  Comparator #(.width(4), .mode("unsigned")) comparator_3 (
    .a(adder_3_out), .b(4'b1001), .gt(comparator_3_gt));  // open: eq, lt
  or or_4 (or_4_out, comparator_1_gt, adder_1_cout);
  or or_5 (or_5_out, comparator_2_gt, adder_2_cout);
  or or_6 (or_6_out, comparator_3_gt, adder_3_cout);
  Multiplexer #(.width(4), .enable("false")) multiplexer_7 (
    .in0(4'b0000), .in1(4'b0110), .out(multiplexer_7_out), .sel(or_4_out));
  Multiplexer #(.width(4), .enable("false")) multiplexer_8 (
    .in0(4'b0000), .in1(4'b0110), .out(multiplexer_8_out), .sel(or_5_out));
  Multiplexer #(.width(4), .enable("false")) multiplexer_9 (
    .in0(4'b0000), .in1(4'b0110), .out(multiplexer_9_out), .sel(or_6_out));
  Adder #(.width(4)) adder_4 (
    .a(adder_1_out), .b(multiplexer_7_out), .out(adder_4_out), .cout(adder_4_cout));  // open: cin
  Adder #(.width(4)) adder_5 (
    .a(adder_2_out), .b(multiplexer_8_out), .out(adder_5_out), .cout(adder_5_cout));  // open: cin
  Adder #(.width(4)) adder_6 (
    .a(adder_3_out), .b(multiplexer_9_out), .out(adder_6_out), .cout(adder_6_cout));  // open: cin
  assign bit_extender_1_out = {{3{1'b0}}, or_3_out};  // Bit_Extender bit_extender_1
  Adder #(.width(4)) adder_7 (.a(4'b0000), .b(adder_4_out), .out(adder_7_out), .cout(adder_7_cout));  // open: cin
  or or_7 (or_7_out, adder_7_cout, adder_13_cout);
  Adder #(.width(4)) adder_8 (.a(4'b0000), .b(adder_5_out), .out(adder_8_out), .cin(or_7_out), .cout(adder_8_cout));
  or or_8 (or_8_out, adder_8_cout, adder_14_cout);
  Adder #(.width(4)) adder_9 (.a(4'b0111), .b(adder_6_out), .out(adder_9_out), .cin(or_8_out), .cout(adder_9_cout));
  or or_9 (or_9_out, adder_9_cout, adder_11_cout);
  Adder #(.width(4)) adder_10 (
    .a(4'b0000), .b(bit_extender_1_out), .out(adder_10_out), .cin(or_9_out), .cout(adder_10_cout));
  Comparator #(.width(4), .mode("unsigned")) comparator_4 (
    .a(adder_7_out), .b(4'b1001), .gt(comparator_4_gt));  // open: eq, lt
  Comparator #(.width(4), .mode("unsigned")) comparator_5 (
    .a(adder_8_out), .b(4'b1001), .gt(comparator_5_gt));  // open: eq, lt
  Comparator #(.width(4), .mode("unsigned")) comparator_6 (
    .a(adder_9_out), .b(4'b1001), .gt(comparator_6_gt));  // open: eq, lt
  Comparator #(.width(4), .mode("unsigned")) comparator_7 (
    .a(adder_10_out), .b(4'b1001), .gt(comparator_7_gt));  // open: eq, lt
  or or_10 (or_10_out, comparator_7_gt, adder_10_cout);
  Multiplexer #(.width(4), .enable("false")) multiplexer_10 (
    .in0(4'b0000), .in1(4'b0110), .out(multiplexer_10_out), .sel(or_11_out));
  or or_11 (or_11_out, comparator_4_gt, adder_7_cout);
  or or_12 (or_12_out, comparator_5_gt, adder_8_cout);
  Multiplexer #(.width(4), .enable("false")) multiplexer_11 (
    .in0(4'b0000), .in1(4'b0110), .out(multiplexer_11_out), .sel(or_13_out));
  or or_13 (or_13_out, comparator_6_gt, adder_9_cout);
  Multiplexer #(.width(4), .enable("false")) multiplexer_12 (
    .in0(4'b0000), .in1(4'b0110), .out(multiplexer_12_out), .sel(or_10_out));
  Multiplexer #(.width(4), .enable("false")) multiplexer_13 (
    .in0(4'b0000), .in1(4'b0110), .out(multiplexer_13_out), .sel(or_12_out));
  Adder #(.width(4)) adder_11 (
    .a(adder_9_out), .b(multiplexer_11_out), .out(adder_11_out), .cout(adder_11_cout));  // open: cin
  Adder #(.width(4)) adder_12 (
    .a(adder_10_out), .b(multiplexer_12_out), .out(adder_12_out), .cout(adder_12_cout));  // open: cin
  Adder #(.width(4)) adder_13 (
    .a(adder_7_out), .b(multiplexer_10_out), .out(adder_13_out), .cout(adder_13_cout));  // open: cin
  Adder #(.width(4)) adder_14 (
    .a(adder_8_out), .b(multiplexer_13_out), .out(adder_14_out), .cout(adder_14_cout));  // open: cin
  assign bit_extender_2_out = {{3{1'b0}}, adder_12_cout};  // Bit_Extender bit_extender_2
  assign bit_extender_3_out = {{1{1'b0}}, Number_of_days};  // Bit_Extender bit_extender_3
  Multiplier #(.width(4)) multiplier_1 (
    .a(adder_13_out), .b(bit_extender_3_out), .out(multiplier_1_out), .cout(multiplier_1_cout));  // open: cin
  Multiplier #(.width(4)) multiplier_2 (
    .a(bit_extender_3_out), .b(adder_14_out), .out(multiplier_2_out), .cout(multiplier_2_cout));  // open: cin
  Multiplier #(.width(4)) multiplier_3 (
    .a(bit_extender_3_out), .b(adder_11_out), .out(multiplier_3_out), .cout(multiplier_3_cout));  // open: cin
  Multiplier #(.width(4)) multiplier_4 (
    .a(bit_extender_3_out), .b(adder_12_out), .out(multiplier_4_out), .cout(multiplier_4_cout));  // open: cin
  Multiplier #(.width(4)) multiplier_5 (
    .a(bit_extender_3_out), .b(bit_extender_2_out), .out(multiplier_5_out), .cout(multiplier_5_cout));  // open: cin
  assign bit_extender_4_out = {{3{1'b0}}, multiplier_1_out};  // Bit_Extender bit_extender_4
  assign bit_extender_5_out = {{3{1'b0}}, multiplier_1_cout};  // Bit_Extender bit_extender_5
  assign bit_extender_6_out = {{3{1'b0}}, multiplier_2_out};  // Bit_Extender bit_extender_6
  assign bit_extender_7_out = {{3{1'b0}}, multiplier_2_cout};  // Bit_Extender bit_extender_7
  assign bit_extender_8_out = {{3{1'b0}}, multiplier_3_out};  // Bit_Extender bit_extender_8
  assign bit_extender_9_out = {{3{1'b0}}, multiplier_3_cout};  // Bit_Extender bit_extender_9
  assign bit_extender_10_out = {{3{1'b0}}, multiplier_4_out};  // Bit_Extender bit_extender_10
  assign bit_extender_11_out = {{3{1'b0}}, multiplier_4_cout};  // Bit_Extender bit_extender_11
  assign bit_extender_12_out = {{3{1'b0}}, multiplier_5_out};  // Bit_Extender bit_extender_12
  assign bit_extender_13_out = {{3{1'b0}}, multiplier_5_cout};  // Bit_Extender bit_extender_13
  Shifter #(.width(7)) shifter_1 (.in(bit_extender_5_out), .\dist (3'b100), .out(shifter_1_out));
  Shifter #(.width(7)) shifter_2 (.in(bit_extender_7_out), .\dist (3'b100), .out(shifter_2_out));
  Shifter #(.width(7)) shifter_3 (.in(bit_extender_9_out), .\dist (3'b100), .out(shifter_3_out));
  Shifter #(.width(7)) shifter_4 (.in(bit_extender_11_out), .\dist (3'b100), .out(shifter_4_out));
  Shifter #(.width(7)) shifter_5 (.in(bit_extender_13_out), .\dist (3'b100), .out(shifter_5_out));
  _7_bit_binary_to_BCD_converter u_7_bit_binary_to_bcd_converter_1 (
    .Output_LSB(n7_bit_binary_to_bcd_converter_1_output_lsb),
    .Output_MSB(n7_bit_binary_to_bcd_converter_1_output_msb), ._7_bit_binary_input(adder_15_out));
  Adder #(.width(7)) adder_15 (.a(bit_extender_4_out), .b(shifter_1_out), .out(adder_15_out));  // open: cin, cout
  Adder #(.width(7)) adder_16 (.a(bit_extender_6_out), .b(shifter_2_out), .out(adder_16_out));  // open: cin, cout
  _7_bit_binary_to_BCD_converter u_7_bit_binary_to_bcd_converter_2 (
    .Output_LSB(n7_bit_binary_to_bcd_converter_2_output_lsb),
    .Output_MSB(n7_bit_binary_to_bcd_converter_2_output_msb), ._7_bit_binary_input(adder_16_out));
  Adder #(.width(7)) adder_17 (.a(bit_extender_8_out), .b(shifter_3_out), .out(adder_17_out));  // open: cin, cout
  _7_bit_binary_to_BCD_converter u_7_bit_binary_to_bcd_converter_3 (
    .Output_LSB(n7_bit_binary_to_bcd_converter_3_output_lsb),
    .Output_MSB(n7_bit_binary_to_bcd_converter_3_output_msb), ._7_bit_binary_input(adder_17_out));
  Adder #(.width(7)) adder_18 (.a(bit_extender_10_out), .b(shifter_4_out), .out(adder_18_out));  // open: cin, cout
  _7_bit_binary_to_BCD_converter u_7_bit_binary_to_bcd_converter_4 (
    .Output_LSB(n7_bit_binary_to_bcd_converter_4_output_lsb),
    .Output_MSB(n7_bit_binary_to_bcd_converter_4_output_msb), ._7_bit_binary_input(adder_18_out));
  Adder #(.width(7)) adder_19 (.a(bit_extender_12_out), .b(shifter_5_out), .out(adder_19_out));  // open: cin, cout
  _7_bit_binary_to_BCD_converter u_7_bit_binary_to_bcd_converter_5 (
    .Output_LSB(n7_bit_binary_to_bcd_converter_5_output_lsb), ._7_bit_binary_input(adder_19_out));  // open: Output_MSB
  Adder #(.width(4)) adder_20 (
    .a(n7_bit_binary_to_bcd_converter_1_output_lsb), .b(4'b0000), .out(adder_20_out), .cout(adder_20_cout));  // open: cin
  or or_14 (or_14_out, adder_20_cout, adder_25_cout);
  Adder #(.width(4)) adder_21 (
    .a(n7_bit_binary_to_bcd_converter_1_output_msb), .b(n7_bit_binary_to_bcd_converter_2_output_lsb),
    .out(adder_21_out), .cin(or_14_out), .cout(adder_21_cout));
  or or_15 (or_15_out, adder_21_cout, adder_26_cout);
  Adder #(.width(4)) adder_22 (
    .a(n7_bit_binary_to_bcd_converter_2_output_msb), .b(n7_bit_binary_to_bcd_converter_3_output_lsb),
    .out(adder_22_out), .cin(or_15_out), .cout(adder_22_cout));
  or or_16 (or_16_out, adder_22_cout, adder_27_cout);
  Adder #(.width(4)) adder_23 (
    .a(n7_bit_binary_to_bcd_converter_3_output_msb), .b(n7_bit_binary_to_bcd_converter_4_output_lsb),
    .out(adder_23_out), .cin(or_16_out), .cout(adder_23_cout));
  or or_17 (or_17_out, adder_23_cout, adder_28_cout);
  Adder #(.width(4)) adder_24 (
    .a(n7_bit_binary_to_bcd_converter_4_output_msb), .b(n7_bit_binary_to_bcd_converter_5_output_lsb),
    .out(adder_24_out), .cin(or_17_out), .cout(adder_24_cout));
  Comparator #(.width(4), .mode("unsigned")) comparator_8 (
    .a(adder_20_out), .b(4'b1001), .gt(comparator_8_gt));  // open: eq, lt
  Comparator #(.width(4), .mode("unsigned")) comparator_9 (
    .a(adder_21_out), .b(4'b1001), .gt(comparator_9_gt));  // open: eq, lt
  Comparator #(.width(4), .mode("unsigned")) comparator_10 (
    .a(adder_22_out), .b(4'b1001), .gt(comparator_10_gt));  // open: eq, lt
  Comparator #(.width(4), .mode("unsigned")) comparator_11 (
    .a(adder_23_out), .b(4'b1001), .gt(comparator_11_gt));  // open: eq, lt
  Comparator #(.width(4), .mode("unsigned")) comparator_12 (
    .a(adder_24_out), .b(4'b1001), .gt(comparator_12_gt));  // open: eq, lt
  or or_18 (or_18_out, comparator_8_gt, adder_20_cout);
  or or_19 (or_19_out, comparator_9_gt, adder_21_cout);
  or or_20 (or_20_out, comparator_10_gt, adder_22_cout);
  or or_21 (or_21_out, comparator_11_gt, adder_23_cout);
  or or_22 (or_22_out, comparator_12_gt, adder_24_cout);
  Multiplexer #(.width(4), .enable("false")) multiplexer_14 (
    .in0(4'b0000), .in1(4'b0110), .out(multiplexer_14_out), .sel(or_18_out));
  Multiplexer #(.width(4), .enable("false")) multiplexer_15 (
    .in0(4'b0000), .in1(4'b0110), .out(multiplexer_15_out), .sel(or_19_out));
  Multiplexer #(.width(4), .enable("false")) multiplexer_16 (
    .in0(4'b0000), .in1(4'b0110), .out(multiplexer_16_out), .sel(or_20_out));
  Multiplexer #(.width(4), .enable("false")) multiplexer_17 (
    .in0(4'b0000), .in1(4'b0110), .out(multiplexer_17_out), .sel(or_21_out));
  Multiplexer #(.width(4), .enable("false")) multiplexer_18 (
    .in0(4'b0000), .in1(4'b0110), .out(multiplexer_18_out), .sel(or_22_out));
  Adder #(.width(4)) adder_25 (.a(adder_20_out), .b(multiplexer_14_out), .out(LSB), .cout(adder_25_cout));  // open: cin
  Adder #(.width(4)) adder_26 (
    .a(adder_21_out), .b(multiplexer_15_out), .out(out_5), .cout(adder_26_cout));  // open: cin
  Adder #(.width(4)) adder_27 (
    .a(adder_22_out), .b(multiplexer_16_out), .out(out_6), .cout(adder_27_cout));  // open: cin
  Adder #(.width(4)) adder_28 (
    .a(adder_23_out), .b(multiplexer_17_out), .out(out_7), .cout(adder_28_cout));  // open: cin
  Adder #(.width(4)) adder_29 (.a(adder_24_out), .b(multiplexer_18_out), .out(MSB));  // open: cin, cout

  // Notes on the sheet:
  //   AC charges
  //   LSB
  //   MSB
  //   Wi-Fi charges
  //   LSB
  //   MSB
  //   AC+Wi-Fi charges adder 
  //   LSB
  //   MSB
  //   Room charges
  //   AC+Wi-Fi+room charges adder
  //   Multiply one day charges and number of days
  //   7 bit binary to BCD converter
  //   7 bit binary to BCD converter
  //   7 bit binary to BCD converter
  //   7 bit binary to BCD converter
  //   7 bit binary to BCD converter
  //   Convert into BCD
  //   Total bill
endmodule

module Bill_calculator_module_for_double_sharing_ac_room (
  input  [2:0] Customer_1_number_of_days_selection,
  input  Customer_1_Wi_Fi_selection,
  input  [2:0] Customer_2_number_of_days_selection,
  input  Customer_2_Wi_Fi_selection,
  output [3:0] LSB,
  output [3:0] out_6,
  output [3:0] out_7,
  output [3:0] out_8,
  output [3:0] MSB,
  output [3:0] LSB_2,
  output [3:0] out_11,
  output [3:0] out_12,
  output [3:0] out_13,
  output [3:0] MSB_2
);

  wire adder_1_cout, adder_2_cout, adder_3_cout, adder_4_cout, adder_5_cout, adder_6_cout, adder_7_cout,
       adder_8_cout, adder_9_cout, adder_10_cout, adder_11_cout, adder_12_cout, adder_16_cout, adder_20_cout,
       adder_21_cout, adder_22_cout, adder_23_cout, adder_24_cout, adder_25_cout, adder_26_cout,
       adder_27_cout, adder_28_cout, adder_29_cout, adder_30_cout, adder_32_cout, adder_33_cout,
       adder_34_cout, adder_35_cout, adder_36_cout, adder_37_cout, adder_38_cout, adder_39_cout,
       comparator_1_gt, comparator_2_gt, comparator_3_gt, comparator_4_gt, comparator_5_gt, comparator_6_gt,
       comparator_7_gt, comparator_8_gt, comparator_9_gt, comparator_10_gt, comparator_11_gt,
       comparator_12_gt, comparator_13_gt, comparator_14_gt, comparator_15_gt, comparator_16_gt, or_1_out,
       or_2_out, or_3_out, or_4_out, or_5_out, or_6_out, or_7_out, or_8_out, or_9_out, or_10_out, or_11_out,
       or_12_out, or_13_out, or_14_out, or_15_out, or_16_out, or_17_out, or_18_out, or_19_out, or_20_out,
       or_21_out, or_22_out, or_23_out, or_24_out, or_25_out, or_26_out, or_27_out, or_28_out, or_29_out,
       or_30_out;
  wire [3:0] adder_1_out, adder_2_out, adder_3_out, adder_4_out, adder_5_out, adder_6_out, adder_7_out,
       adder_8_out, adder_9_out, adder_10_out, adder_11_out, adder_12_out, adder_21_out, adder_22_out,
       adder_23_out, adder_24_out, adder_25_out, adder_26_out, adder_27_out, adder_28_out, adder_29_out,
       adder_30_out, bit_extender_1_out, bit_extender_2_out, bit_extender_3_out, bit_extender_4_out,
       bit_extender_21_out, bit_extender_22_out, multiplexer_1_out, multiplexer_2_out, multiplexer_3_out,
       multiplexer_4_out, multiplexer_5_out, multiplexer_6_out, multiplexer_7_out, multiplexer_8_out,
       multiplexer_9_out, multiplexer_10_out, multiplexer_11_out, multiplexer_12_out, multiplexer_13_out,
       multiplexer_14_out, multiplexer_15_out, multiplexer_16_out, multiplexer_17_out, multiplexer_18_out,
       multiplexer_19_out, multiplexer_20_out, multiplexer_21_out, multiplexer_22_out, multiplier_1_cout,
       multiplier_1_out, multiplier_2_cout, multiplier_2_out, multiplier_3_cout, multiplier_3_out,
       multiplier_4_cout, multiplier_4_out, multiplier_5_cout, multiplier_5_out, multiplier_6_cout,
       multiplier_6_out, multiplier_7_cout, multiplier_7_out, multiplier_8_cout, multiplier_8_out,
       n7_bit_binary_to_bcd_converter_1_output_lsb, n7_bit_binary_to_bcd_converter_1_output_msb,
       n7_bit_binary_to_bcd_converter_2_output_lsb, n7_bit_binary_to_bcd_converter_2_output_msb,
       n7_bit_binary_to_bcd_converter_3_output_lsb, n7_bit_binary_to_bcd_converter_3_output_msb,
       n7_bit_binary_to_bcd_converter_4_output_lsb, n7_bit_binary_to_bcd_converter_4_output_msb,
       n7_bit_binary_to_bcd_converter_5_output_lsb, n7_bit_binary_to_bcd_converter_5_output_msb,
       n7_bit_binary_to_bcd_converter_6_output_lsb, n7_bit_binary_to_bcd_converter_6_output_msb,
       n7_bit_binary_to_bcd_converter_7_output_lsb, n7_bit_binary_to_bcd_converter_7_output_msb,
       n7_bit_binary_to_bcd_converter_8_output_lsb, n7_bit_binary_to_bcd_converter_8_output_msb;
  wire [6:0] adder_13_out, adder_14_out, adder_15_out, adder_16_out, adder_17_out, adder_18_out,
       adder_19_out, adder_20_out, bit_extender_5_out, bit_extender_6_out, bit_extender_7_out,
       bit_extender_8_out, bit_extender_9_out, bit_extender_10_out, bit_extender_11_out, bit_extender_12_out,
       bit_extender_13_out, bit_extender_14_out, bit_extender_15_out, bit_extender_16_out,
       bit_extender_17_out, bit_extender_18_out, bit_extender_19_out, bit_extender_20_out, shifter_1_out,
       shifter_2_out, shifter_3_out, shifter_4_out, shifter_5_out, shifter_6_out, shifter_7_out,
       shifter_8_out;

  Multiplexer #(.width(4), .enable("false")) multiplexer_1 (
    .in0(4'b0000), .in1(4'b0000), .out(multiplexer_1_out), .sel(Customer_1_Wi_Fi_selection));
  Multiplexer #(.width(4), .enable("false")) multiplexer_2 (
    .in0(4'b0000), .in1(4'b0000), .out(multiplexer_2_out), .sel(Customer_1_Wi_Fi_selection));
  Multiplexer #(.width(4), .enable("false")) multiplexer_3 (
    .in0(4'b0000), .in1(4'b0001), .out(multiplexer_3_out), .sel(Customer_1_Wi_Fi_selection));
  Multiplexer #(.width(4), .enable("false")) multiplexer_4 (
    .in0(4'b0000), .in1(4'b0000), .out(multiplexer_4_out), .sel(Customer_2_Wi_Fi_selection));
  Multiplexer #(.width(4), .enable("false")) multiplexer_5 (
    .in0(4'b0000), .in1(4'b0000), .out(multiplexer_5_out), .sel(Customer_2_Wi_Fi_selection));
  Multiplexer #(.width(4), .enable("false")) multiplexer_6 (
    .in0(4'b0000), .in1(4'b0001), .out(multiplexer_6_out), .sel(Customer_2_Wi_Fi_selection));
  Adder #(.width(4)) adder_1 (.a(4'b0000), .b(multiplexer_1_out), .out(adder_1_out), .cout(adder_1_cout));  // open: cin
  or or_1 (or_1_out, adder_1_cout, adder_7_cout);
  Adder #(.width(4)) adder_2 (
    .a(4'b0000), .b(multiplexer_2_out), .out(adder_2_out), .cin(or_1_out), .cout(adder_2_cout));
  or or_2 (or_2_out, adder_2_cout, adder_8_cout);
  Adder #(.width(4)) adder_3 (
    .a(4'b0110), .b(multiplexer_3_out), .out(adder_3_out), .cin(or_2_out), .cout(adder_3_cout));
  or or_3 (or_3_out, adder_3_cout, adder_9_cout);
  or or_4 (or_4_out, adder_4_cout, adder_10_cout);
  or or_5 (or_5_out, adder_5_cout, adder_11_cout);
  Comparator #(.width(4), .mode("unsigned")) comparator_1 (
    .a(adder_1_out), .b(4'b1001), .gt(comparator_1_gt));  // open: eq, lt
  Comparator #(.width(4), .mode("unsigned")) comparator_2 (
    .a(adder_2_out), .b(4'b1001), .gt(comparator_2_gt));  // open: eq, lt
  Adder #(.width(4)) adder_4 (.a(4'b0000), .b(multiplexer_4_out), .out(adder_4_out), .cout(adder_4_cout));  // open: cin
  Adder #(.width(4)) adder_5 (
    .a(4'b0000), .b(multiplexer_5_out), .out(adder_5_out), .cin(or_4_out), .cout(adder_5_cout));
  Adder #(.width(4)) adder_6 (
    .a(4'b0110), .b(multiplexer_6_out), .out(adder_6_out), .cin(or_5_out), .cout(adder_6_cout));
  or or_6 (or_6_out, adder_6_cout, adder_12_cout);
  Comparator #(.width(4), .mode("unsigned")) comparator_3 (
    .a(adder_3_out), .b(4'b1001), .gt(comparator_3_gt));  // open: eq, lt
  Comparator #(.width(4), .mode("unsigned")) comparator_4 (
    .a(adder_4_out), .b(4'b1001), .gt(comparator_4_gt));  // open: eq, lt
  Comparator #(.width(4), .mode("unsigned")) comparator_5 (
    .a(adder_5_out), .b(4'b1001), .gt(comparator_5_gt));  // open: eq, lt
  Comparator #(.width(4), .mode("unsigned")) comparator_6 (
    .a(adder_6_out), .b(4'b1001), .gt(comparator_6_gt));  // open: eq, lt
  or or_7 (or_7_out, comparator_1_gt, adder_1_cout);
  or or_8 (or_8_out, comparator_2_gt, adder_2_cout);
  or or_9 (or_9_out, comparator_3_gt, adder_3_cout);
  or or_10 (or_10_out, comparator_4_gt, adder_4_cout);
  or or_11 (or_11_out, comparator_5_gt, adder_5_cout);
  or or_12 (or_12_out, comparator_6_gt, adder_6_cout);
  Multiplexer #(.width(4), .enable("false")) multiplexer_7 (
    .in0(4'b0000), .in1(4'b0110), .out(multiplexer_7_out), .sel(or_7_out));
  Multiplexer #(.width(4), .enable("false")) multiplexer_8 (
    .in0(4'b0000), .in1(4'b0110), .out(multiplexer_8_out), .sel(or_8_out));
  Multiplexer #(.width(4), .enable("false")) multiplexer_9 (
    .in0(4'b0000), .in1(4'b0110), .out(multiplexer_9_out), .sel(or_9_out));
  Multiplexer #(.width(4), .enable("false")) multiplexer_10 (
    .in0(4'b0000), .in1(4'b0110), .out(multiplexer_10_out), .sel(or_10_out));
  Multiplexer #(.width(4), .enable("false")) multiplexer_11 (
    .in0(4'b0000), .in1(4'b0110), .out(multiplexer_11_out), .sel(or_11_out));
  Multiplexer #(.width(4), .enable("false")) multiplexer_12 (
    .in0(4'b0000), .in1(4'b0110), .out(multiplexer_12_out), .sel(or_12_out));
  Adder #(.width(4)) adder_7 (
    .a(adder_1_out), .b(multiplexer_7_out), .out(adder_7_out), .cout(adder_7_cout));  // open: cin
  assign bit_extender_1_out = {{1{1'b0}}, Customer_1_number_of_days_selection};  // Bit_Extender bit_extender_1
  Adder #(.width(4)) adder_8 (
    .a(adder_2_out), .b(multiplexer_8_out), .out(adder_8_out), .cout(adder_8_cout));  // open: cin
  Adder #(.width(4)) adder_9 (
    .a(adder_3_out), .b(multiplexer_9_out), .out(adder_9_out), .cout(adder_9_cout));  // open: cin
  Adder #(.width(4)) adder_10 (
    .a(adder_4_out), .b(multiplexer_10_out), .out(adder_10_out), .cout(adder_10_cout));  // open: cin
  Adder #(.width(4)) adder_11 (
    .a(adder_5_out), .b(multiplexer_11_out), .out(adder_11_out), .cout(adder_11_cout));  // open: cin
  Adder #(.width(4)) adder_12 (
    .a(adder_6_out), .b(multiplexer_12_out), .out(adder_12_out), .cout(adder_12_cout));  // open: cin
  assign bit_extender_2_out = {{3{1'b0}}, or_3_out};  // Bit_Extender bit_extender_2
  assign bit_extender_3_out = {{1{1'b0}}, Customer_2_number_of_days_selection};  // Bit_Extender bit_extender_3
  assign bit_extender_4_out = {{3{1'b0}}, or_6_out};  // Bit_Extender bit_extender_4
  Multiplier #(.width(4)) multiplier_1 (
    .a(adder_7_out), .b(bit_extender_1_out), .out(multiplier_1_out), .cout(multiplier_1_cout));  // open: cin
  Multiplier #(.width(4)) multiplier_2 (
    .a(bit_extender_1_out), .b(adder_8_out), .out(multiplier_2_out), .cout(multiplier_2_cout));  // open: cin
  Multiplier #(.width(4)) multiplier_3 (
    .a(bit_extender_1_out), .b(adder_9_out), .out(multiplier_3_out), .cout(multiplier_3_cout));  // open: cin
  Multiplier #(.width(4)) multiplier_4 (
    .a(bit_extender_1_out), .b(bit_extender_2_out), .out(multiplier_4_out), .cout(multiplier_4_cout));  // open: cin
  Multiplier #(.width(4)) multiplier_5 (
    .a(adder_10_out), .b(bit_extender_3_out), .out(multiplier_5_out), .cout(multiplier_5_cout));  // open: cin
  Multiplier #(.width(4)) multiplier_6 (
    .a(bit_extender_3_out), .b(adder_11_out), .out(multiplier_6_out), .cout(multiplier_6_cout));  // open: cin
  Multiplier #(.width(4)) multiplier_7 (
    .a(bit_extender_3_out), .b(adder_12_out), .out(multiplier_7_out), .cout(multiplier_7_cout));  // open: cin
  Multiplier #(.width(4)) multiplier_8 (
    .a(bit_extender_3_out), .b(bit_extender_4_out), .out(multiplier_8_out), .cout(multiplier_8_cout));  // open: cin
  assign bit_extender_5_out = {{3{1'b0}}, multiplier_1_out};  // Bit_Extender bit_extender_5
  assign bit_extender_6_out = {{3{1'b0}}, multiplier_1_cout};  // Bit_Extender bit_extender_6
  assign bit_extender_7_out = {{3{1'b0}}, multiplier_2_out};  // Bit_Extender bit_extender_7
  assign bit_extender_8_out = {{3{1'b0}}, multiplier_2_cout};  // Bit_Extender bit_extender_8
  assign bit_extender_9_out = {{3{1'b0}}, multiplier_3_out};  // Bit_Extender bit_extender_9
  assign bit_extender_10_out = {{3{1'b0}}, multiplier_3_cout};  // Bit_Extender bit_extender_10
  assign bit_extender_11_out = {{3{1'b0}}, multiplier_4_out};  // Bit_Extender bit_extender_11
  assign bit_extender_12_out = {{3{1'b0}}, multiplier_4_cout};  // Bit_Extender bit_extender_12
  assign bit_extender_13_out = {{3{1'b0}}, multiplier_5_out};  // Bit_Extender bit_extender_13
  assign bit_extender_14_out = {{3{1'b0}}, multiplier_5_cout};  // Bit_Extender bit_extender_14
  assign bit_extender_15_out = {{3{1'b0}}, multiplier_6_out};  // Bit_Extender bit_extender_15
  assign bit_extender_16_out = {{3{1'b0}}, multiplier_6_cout};  // Bit_Extender bit_extender_16
  assign bit_extender_17_out = {{3{1'b0}}, multiplier_7_out};  // Bit_Extender bit_extender_17
  assign bit_extender_18_out = {{3{1'b0}}, multiplier_7_cout};  // Bit_Extender bit_extender_18
  assign bit_extender_19_out = {{3{1'b0}}, multiplier_8_out};  // Bit_Extender bit_extender_19
  assign bit_extender_20_out = {{3{1'b0}}, multiplier_8_cout};  // Bit_Extender bit_extender_20
  Shifter #(.width(7)) shifter_1 (.in(bit_extender_6_out), .\dist (3'b100), .out(shifter_1_out));
  Shifter #(.width(7)) shifter_2 (.in(bit_extender_8_out), .\dist (3'b100), .out(shifter_2_out));
  Shifter #(.width(7)) shifter_3 (.in(bit_extender_10_out), .\dist (3'b100), .out(shifter_3_out));
  Shifter #(.width(7)) shifter_4 (.in(bit_extender_12_out), .\dist (3'b100), .out(shifter_4_out));
  Shifter #(.width(7)) shifter_5 (.in(bit_extender_14_out), .\dist (3'b100), .out(shifter_5_out));
  Shifter #(.width(7)) shifter_6 (.in(bit_extender_16_out), .\dist (3'b100), .out(shifter_6_out));
  Shifter #(.width(7)) shifter_7 (.in(bit_extender_18_out), .\dist (3'b100), .out(shifter_7_out));
  Shifter #(.width(7)) shifter_8 (.in(bit_extender_20_out), .\dist (3'b100), .out(shifter_8_out));
  Adder #(.width(7)) adder_13 (.a(bit_extender_5_out), .b(shifter_1_out), .out(adder_13_out));  // open: cin, cout
  Adder #(.width(7)) adder_14 (.a(bit_extender_7_out), .b(shifter_2_out), .out(adder_14_out));  // open: cin, cout
  Adder #(.width(7)) adder_15 (.a(bit_extender_9_out), .b(shifter_3_out), .out(adder_15_out));  // open: cin, cout
  Adder #(.width(7)) adder_16 (
    .a(bit_extender_11_out), .b(shifter_4_out), .out(adder_16_out), .cout(adder_16_cout));  // open: cin
  Adder #(.width(7)) adder_17 (.a(bit_extender_13_out), .b(shifter_5_out), .out(adder_17_out));  // open: cin, cout
  Adder #(.width(7)) adder_18 (.a(bit_extender_15_out), .b(shifter_6_out), .out(adder_18_out));  // open: cin, cout
  Adder #(.width(7)) adder_19 (.a(bit_extender_17_out), .b(shifter_7_out), .out(adder_19_out));  // open: cin, cout
  Adder #(.width(7)) adder_20 (
    .a(bit_extender_19_out), .b(shifter_8_out), .out(adder_20_out), .cout(adder_20_cout));  // open: cin
  _7_bit_binary_to_BCD_converter u_7_bit_binary_to_bcd_converter_1 (
    .Output_LSB(n7_bit_binary_to_bcd_converter_1_output_lsb),
    .Output_MSB(n7_bit_binary_to_bcd_converter_1_output_msb), ._7_bit_binary_input(adder_13_out));
  _7_bit_binary_to_BCD_converter u_7_bit_binary_to_bcd_converter_2 (
    .Output_LSB(n7_bit_binary_to_bcd_converter_2_output_lsb),
    .Output_MSB(n7_bit_binary_to_bcd_converter_2_output_msb), ._7_bit_binary_input(adder_14_out));
  _7_bit_binary_to_BCD_converter u_7_bit_binary_to_bcd_converter_3 (
    .Output_LSB(n7_bit_binary_to_bcd_converter_3_output_lsb),
    .Output_MSB(n7_bit_binary_to_bcd_converter_3_output_msb), ._7_bit_binary_input(adder_15_out));
  _7_bit_binary_to_BCD_converter u_7_bit_binary_to_bcd_converter_4 (
    .Output_LSB(n7_bit_binary_to_bcd_converter_4_output_lsb),
    .Output_MSB(n7_bit_binary_to_bcd_converter_4_output_msb), ._7_bit_binary_input(adder_16_out));
  assign bit_extender_21_out = {{3{1'b0}}, adder_16_cout};  // Bit_Extender bit_extender_21
  _7_bit_binary_to_BCD_converter u_7_bit_binary_to_bcd_converter_5 (
    .Output_LSB(n7_bit_binary_to_bcd_converter_5_output_lsb),
    .Output_MSB(n7_bit_binary_to_bcd_converter_5_output_msb), ._7_bit_binary_input(adder_17_out));
  _7_bit_binary_to_BCD_converter u_7_bit_binary_to_bcd_converter_6 (
    .Output_LSB(n7_bit_binary_to_bcd_converter_6_output_lsb),
    .Output_MSB(n7_bit_binary_to_bcd_converter_6_output_msb), ._7_bit_binary_input(adder_18_out));
  _7_bit_binary_to_BCD_converter u_7_bit_binary_to_bcd_converter_7 (
    .Output_LSB(n7_bit_binary_to_bcd_converter_7_output_lsb),
    .Output_MSB(n7_bit_binary_to_bcd_converter_7_output_msb), ._7_bit_binary_input(adder_19_out));
  _7_bit_binary_to_BCD_converter u_7_bit_binary_to_bcd_converter_8 (
    .Output_LSB(n7_bit_binary_to_bcd_converter_8_output_lsb),
    .Output_MSB(n7_bit_binary_to_bcd_converter_8_output_msb), ._7_bit_binary_input(adder_20_out));
  assign bit_extender_22_out = {{3{1'b0}}, adder_20_cout};  // Bit_Extender bit_extender_22
  or or_13 (or_13_out, adder_21_cout, adder_32_cout);
  or or_14 (or_14_out, adder_22_cout, adder_33_cout);
  or or_15 (or_15_out, adder_23_cout, adder_34_cout);
  Adder #(.width(4)) adder_21 (
    .a(n7_bit_binary_to_bcd_converter_1_output_lsb), .b(4'b0000), .out(adder_21_out), .cout(adder_21_cout));  // open: cin
  Adder #(.width(4)) adder_22 (
    .a(n7_bit_binary_to_bcd_converter_1_output_msb), .b(n7_bit_binary_to_bcd_converter_2_output_lsb),
    .out(adder_22_out), .cin(or_13_out), .cout(adder_22_cout));
  Adder #(.width(4)) adder_23 (
    .a(n7_bit_binary_to_bcd_converter_2_output_msb), .b(n7_bit_binary_to_bcd_converter_3_output_lsb),
    .out(adder_23_out), .cin(or_14_out), .cout(adder_23_cout));
  Adder #(.width(4)) adder_24 (
    .a(n7_bit_binary_to_bcd_converter_3_output_msb), .b(n7_bit_binary_to_bcd_converter_4_output_lsb),
    .out(adder_24_out), .cin(or_15_out), .cout(adder_24_cout));
  or or_16 (or_16_out, adder_24_cout, adder_35_cout);
  Adder #(.width(4)) adder_25 (
    .a(n7_bit_binary_to_bcd_converter_4_output_msb), .b(bit_extender_21_out), .out(adder_25_out),
    .cin(or_16_out), .cout(adder_25_cout));
  Adder #(.width(4)) adder_26 (
    .a(n7_bit_binary_to_bcd_converter_5_output_lsb), .b(4'b0000), .out(adder_26_out), .cout(adder_26_cout));  // open: cin
  or or_17 (or_17_out, adder_26_cout, adder_36_cout);
  Adder #(.width(4)) adder_27 (
    .a(n7_bit_binary_to_bcd_converter_5_output_msb), .b(n7_bit_binary_to_bcd_converter_6_output_lsb),
    .out(adder_27_out), .cin(or_17_out), .cout(adder_27_cout));
  or or_18 (or_18_out, adder_27_cout, adder_37_cout);
  Adder #(.width(4)) adder_28 (
    .a(n7_bit_binary_to_bcd_converter_6_output_msb), .b(n7_bit_binary_to_bcd_converter_7_output_lsb),
    .out(adder_28_out), .cin(or_18_out), .cout(adder_28_cout));
  or or_19 (or_19_out, adder_28_cout, adder_38_cout);
  Adder #(.width(4)) adder_29 (
    .a(n7_bit_binary_to_bcd_converter_7_output_msb), .b(n7_bit_binary_to_bcd_converter_8_output_lsb),
    .out(adder_29_out), .cin(or_19_out), .cout(adder_29_cout));
  or or_20 (or_20_out, adder_29_cout, adder_39_cout);
  Adder #(.width(4)) adder_30 (
    .a(n7_bit_binary_to_bcd_converter_8_output_msb), .b(bit_extender_22_out), .out(adder_30_out),
    .cin(or_20_out), .cout(adder_30_cout));
  Comparator #(.width(4), .mode("unsigned")) comparator_7 (
    .a(adder_21_out), .b(4'b1001), .gt(comparator_7_gt));  // open: eq, lt
  Comparator #(.width(4), .mode("unsigned")) comparator_8 (
    .a(adder_22_out), .b(4'b1001), .gt(comparator_8_gt));  // open: eq, lt
  Comparator #(.width(4), .mode("unsigned")) comparator_9 (
    .a(adder_23_out), .b(4'b1001), .gt(comparator_9_gt));  // open: eq, lt
  Comparator #(.width(4), .mode("unsigned")) comparator_10 (
    .a(adder_24_out), .b(4'b1001), .gt(comparator_10_gt));  // open: eq, lt
  Comparator #(.width(4), .mode("unsigned")) comparator_11 (
    .a(adder_25_out), .b(4'b1001), .gt(comparator_11_gt));  // open: eq, lt
  or or_21 (or_21_out, comparator_7_gt, adder_21_cout);
  Comparator #(.width(4), .mode("unsigned")) comparator_12 (
    .a(adder_26_out), .b(4'b1001), .gt(comparator_12_gt));  // open: eq, lt
  Comparator #(.width(4), .mode("unsigned")) comparator_13 (
    .a(adder_27_out), .b(4'b1001), .gt(comparator_13_gt));  // open: eq, lt
  Comparator #(.width(4), .mode("unsigned")) comparator_14 (
    .a(adder_28_out), .b(4'b1001), .gt(comparator_14_gt));  // open: eq, lt
  Comparator #(.width(4), .mode("unsigned")) comparator_15 (
    .a(adder_29_out), .b(4'b1001), .gt(comparator_15_gt));  // open: eq, lt
  Comparator #(.width(4), .mode("unsigned")) comparator_16 (
    .a(adder_30_out), .b(4'b1001), .gt(comparator_16_gt));  // open: eq, lt
  Multiplexer #(.width(4), .enable("false")) multiplexer_13 (
    .in0(4'b0000), .in1(4'b0110), .out(multiplexer_13_out), .sel(or_21_out));
  or or_22 (or_22_out, comparator_8_gt, adder_22_cout);
  or or_23 (or_23_out, comparator_9_gt, adder_23_cout);
  or or_24 (or_24_out, comparator_10_gt, adder_24_cout);
  Multiplexer #(.width(4), .enable("false")) multiplexer_14 (
    .in0(4'b0000), .in1(4'b0110), .out(multiplexer_14_out), .sel(or_25_out));
  or or_25 (or_25_out, comparator_11_gt, adder_25_cout);
  or or_26 (or_26_out, comparator_12_gt, adder_26_cout);
  or or_27 (or_27_out, comparator_13_gt, adder_27_cout);
  or or_28 (or_28_out, comparator_14_gt, adder_28_cout);
  or or_29 (or_29_out, comparator_15_gt, adder_29_cout);
  Multiplexer #(.width(4), .enable("false")) multiplexer_15 (
    .in0(4'b0000), .in1(4'b0110), .out(multiplexer_15_out), .sel(or_22_out));
  Multiplexer #(.width(4), .enable("false")) multiplexer_16 (
    .in0(4'b0000), .in1(4'b0110), .out(multiplexer_16_out), .sel(or_23_out));
  Multiplexer #(.width(4), .enable("false")) multiplexer_17 (
    .in0(4'b0000), .in1(4'b0110), .out(multiplexer_17_out), .sel(or_24_out));
  Adder #(.width(4)) adder_31 (.a(adder_25_out), .b(multiplexer_14_out), .out(MSB));  // open: cin, cout
  Multiplexer #(.width(4), .enable("false")) multiplexer_18 (
    .in0(4'b0000), .in1(4'b0110), .out(multiplexer_18_out), .sel(or_26_out));
  Multiplexer #(.width(4), .enable("false")) multiplexer_19 (
    .in0(4'b0000), .in1(4'b0110), .out(multiplexer_19_out), .sel(or_27_out));
  Multiplexer #(.width(4), .enable("false")) multiplexer_20 (
    .in0(4'b0000), .in1(4'b0110), .out(multiplexer_20_out), .sel(or_28_out));
  Multiplexer #(.width(4), .enable("false")) multiplexer_21 (
    .in0(4'b0000), .in1(4'b0110), .out(multiplexer_21_out), .sel(or_29_out));
  Multiplexer #(.width(4), .enable("false")) multiplexer_22 (
    .in0(4'b0000), .in1(4'b0110), .out(multiplexer_22_out), .sel(or_30_out));
  or or_30 (or_30_out, comparator_16_gt, adder_30_cout);
  Adder #(.width(4)) adder_32 (.a(adder_21_out), .b(multiplexer_13_out), .out(LSB), .cout(adder_32_cout));  // open: cin
  Adder #(.width(4)) adder_33 (
    .a(adder_22_out), .b(multiplexer_15_out), .out(out_6), .cout(adder_33_cout));  // open: cin
  Adder #(.width(4)) adder_34 (
    .a(adder_23_out), .b(multiplexer_16_out), .out(out_7), .cout(adder_34_cout));  // open: cin
  Adder #(.width(4)) adder_35 (
    .a(adder_24_out), .b(multiplexer_17_out), .out(out_8), .cout(adder_35_cout));  // open: cin
  Adder #(.width(4)) adder_36 (
    .a(adder_26_out), .b(multiplexer_18_out), .out(LSB_2), .cout(adder_36_cout));  // open: cin
  Adder #(.width(4)) adder_37 (
    .a(adder_27_out), .b(multiplexer_19_out), .out(out_11), .cout(adder_37_cout));  // open: cin
  Adder #(.width(4)) adder_38 (
    .a(adder_28_out), .b(multiplexer_20_out), .out(out_12), .cout(adder_38_cout));  // open: cin
  Adder #(.width(4)) adder_39 (
    .a(adder_29_out), .b(multiplexer_21_out), .out(out_13), .cout(adder_39_cout));  // open: cin
  Adder #(.width(4)) adder_40 (.a(adder_30_out), .b(multiplexer_22_out), .out(MSB_2));  // open: cin, cout

  // Notes on the sheet:
  //   LSB
  //   MSB
  //   Wi-Fi charges
  //   Room charges
  //   MSB
  //   LSB
  //   Wi-Fi+room charges adder
  //   Wi-Fi+room charges adder
  //   Multiply one day charges and number of days
  //   Multiply one day charges and number of days
  //   7 bit binary to BCD converter
  //   7 bit binary to BCD converter
  //   7 bit binary to BCD converter
  //   7 bit binary to BCD converter
  //   7 bit binary to BCD converter
  //   7 bit binary to BCD converter
  //   7 bit binary to BCD converter
  //   7 bit binary to BCD converter
  //   Convert into BCD
  //   Convert into BCD
  //   Customer-1 total bill
  //   Customer-2 total bill
endmodule

module Bill_calculator_module_for_double_sharing_non_ac_room (
  input  [2:0] Customer_1_number_of_days_selection,
  input  Customer_2_Wi_Fi_selection,
  input  [2:0] Customer_2_number_of_days_selection,
  input  Customer_2_Wi_Fi_selection_2,
  output [3:0] LSB,
  output [3:0] out_6,
  output [3:0] out_7,
  output [3:0] out_8,
  output [3:0] MSB,
  output [3:0] LSB_2,
  output [3:0] out_11,
  output [3:0] out_12,
  output [3:0] out_13,
  output [3:0] MSB_2
);

  wire adder_1_cout, adder_2_cout, adder_3_cout, adder_4_cout, adder_5_cout, adder_6_cout, adder_7_cout,
       adder_8_cout, adder_9_cout, adder_10_cout, adder_11_cout, adder_12_cout, adder_16_cout, adder_20_cout,
       adder_21_cout, adder_22_cout, adder_23_cout, adder_24_cout, adder_25_cout, adder_26_cout,
       adder_27_cout, adder_28_cout, adder_29_cout, adder_30_cout, adder_31_cout, adder_33_cout,
       adder_34_cout, adder_35_cout, adder_36_cout, adder_37_cout, adder_38_cout, adder_39_cout,
       comparator_1_gt, comparator_2_gt, comparator_3_gt, comparator_4_gt, comparator_5_gt, comparator_6_gt,
       comparator_7_gt, comparator_8_gt, comparator_9_gt, comparator_10_gt, comparator_11_gt,
       comparator_12_gt, comparator_13_gt, comparator_14_gt, comparator_15_gt, comparator_16_gt, or_1_out,
       or_2_out, or_3_out, or_4_out, or_5_out, or_6_out, or_7_out, or_8_out, or_9_out, or_10_out, or_11_out,
       or_12_out, or_13_out, or_14_out, or_15_out, or_16_out, or_17_out, or_18_out, or_19_out, or_20_out,
       or_21_out, or_22_out, or_23_out, or_24_out, or_25_out, or_26_out, or_27_out, or_28_out, or_29_out,
       or_30_out;
  wire [3:0] adder_1_out, adder_2_out, adder_3_out, adder_4_out, adder_5_out, adder_6_out, adder_7_out,
       adder_8_out, adder_9_out, adder_10_out, adder_11_out, adder_12_out, adder_21_out, adder_22_out,
       adder_23_out, adder_24_out, adder_25_out, adder_26_out, adder_27_out, adder_28_out, adder_29_out,
       adder_30_out, bit_extender_1_out, bit_extender_2_out, bit_extender_3_out, bit_extender_4_out,
       bit_extender_21_out, bit_extender_22_out, multiplexer_1_out, multiplexer_2_out, multiplexer_3_out,
       multiplexer_4_out, multiplexer_5_out, multiplexer_6_out, multiplexer_7_out, multiplexer_8_out,
       multiplexer_9_out, multiplexer_10_out, multiplexer_11_out, multiplexer_12_out, multiplexer_13_out,
       multiplexer_14_out, multiplexer_15_out, multiplexer_16_out, multiplexer_17_out, multiplexer_18_out,
       multiplexer_19_out, multiplexer_20_out, multiplexer_21_out, multiplexer_22_out, multiplier_1_cout,
       multiplier_1_out, multiplier_2_cout, multiplier_2_out, multiplier_3_cout, multiplier_3_out,
       multiplier_4_cout, multiplier_4_out, multiplier_5_cout, multiplier_5_out, multiplier_6_cout,
       multiplier_6_out, multiplier_7_cout, multiplier_7_out, multiplier_8_cout, multiplier_8_out,
       n7_bit_binary_to_bcd_converter_1_output_lsb, n7_bit_binary_to_bcd_converter_1_output_msb,
       n7_bit_binary_to_bcd_converter_2_output_lsb, n7_bit_binary_to_bcd_converter_2_output_msb,
       n7_bit_binary_to_bcd_converter_3_output_lsb, n7_bit_binary_to_bcd_converter_3_output_msb,
       n7_bit_binary_to_bcd_converter_4_output_lsb, n7_bit_binary_to_bcd_converter_4_output_msb,
       n7_bit_binary_to_bcd_converter_5_output_lsb, n7_bit_binary_to_bcd_converter_5_output_msb,
       n7_bit_binary_to_bcd_converter_6_output_lsb, n7_bit_binary_to_bcd_converter_6_output_msb,
       n7_bit_binary_to_bcd_converter_7_output_lsb, n7_bit_binary_to_bcd_converter_7_output_msb,
       n7_bit_binary_to_bcd_converter_8_output_lsb, n7_bit_binary_to_bcd_converter_8_output_msb;
  wire [6:0] adder_13_out, adder_14_out, adder_15_out, adder_16_out, adder_17_out, adder_18_out,
       adder_19_out, adder_20_out, bit_extender_5_out, bit_extender_6_out, bit_extender_7_out,
       bit_extender_8_out, bit_extender_9_out, bit_extender_10_out, bit_extender_11_out, bit_extender_12_out,
       bit_extender_13_out, bit_extender_14_out, bit_extender_15_out, bit_extender_16_out,
       bit_extender_17_out, bit_extender_18_out, bit_extender_19_out, bit_extender_20_out, shifter_1_out,
       shifter_2_out, shifter_3_out, shifter_4_out, shifter_5_out, shifter_6_out, shifter_7_out,
       shifter_8_out;

  Multiplexer #(.width(4), .enable("false")) multiplexer_1 (
    .in0(4'b0000), .in1(4'b0000), .out(multiplexer_1_out), .sel(Customer_2_Wi_Fi_selection));
  Multiplexer #(.width(4), .enable("false")) multiplexer_2 (
    .in0(4'b0000), .in1(4'b0000), .out(multiplexer_2_out), .sel(Customer_2_Wi_Fi_selection));
  Multiplexer #(.width(4), .enable("false")) multiplexer_3 (
    .in0(4'b0000), .in1(4'b0001), .out(multiplexer_3_out), .sel(Customer_2_Wi_Fi_selection));
  Multiplexer #(.width(4), .enable("false")) multiplexer_4 (
    .in0(4'b0000), .in1(4'b0000), .out(multiplexer_4_out), .sel(Customer_2_Wi_Fi_selection_2));
  Multiplexer #(.width(4), .enable("false")) multiplexer_5 (
    .in0(4'b0000), .in1(4'b0000), .out(multiplexer_5_out), .sel(Customer_2_Wi_Fi_selection_2));
  Multiplexer #(.width(4), .enable("false")) multiplexer_6 (
    .in0(4'b0000), .in1(4'b0001), .out(multiplexer_6_out), .sel(Customer_2_Wi_Fi_selection_2));
  Adder #(.width(4)) adder_1 (.a(4'b0000), .b(multiplexer_1_out), .out(adder_1_out), .cout(adder_1_cout));  // open: cin
  or or_1 (or_1_out, adder_1_cout, adder_7_cout);
  Adder #(.width(4)) adder_2 (
    .a(4'b0000), .b(multiplexer_2_out), .out(adder_2_out), .cin(or_1_out), .cout(adder_2_cout));
  or or_2 (or_2_out, adder_2_cout, adder_8_cout);
  Adder #(.width(4)) adder_3 (
    .a(4'b0100), .b(multiplexer_3_out), .out(adder_3_out), .cin(or_2_out), .cout(adder_3_cout));
  or or_3 (or_3_out, adder_3_cout, adder_9_cout);
  Adder #(.width(4)) adder_4 (.a(4'b0000), .b(multiplexer_4_out), .out(adder_4_out), .cout(adder_4_cout));  // open: cin
  or or_4 (or_4_out, adder_4_cout, adder_10_cout);
  Adder #(.width(4)) adder_5 (
    .a(4'b0000), .b(multiplexer_5_out), .out(adder_5_out), .cin(or_4_out), .cout(adder_5_cout));
  or or_5 (or_5_out, adder_5_cout, adder_11_cout);
  Adder #(.width(4)) adder_6 (
    .a(4'b0100), .b(multiplexer_6_out), .out(adder_6_out), .cin(or_5_out), .cout(adder_6_cout));
  or or_6 (or_6_out, adder_6_cout, adder_12_cout);
  Comparator #(.width(4), .mode("unsigned")) comparator_1 (
    .a(adder_1_out), .b(4'b1001), .gt(comparator_1_gt));  // open: eq, lt
  Comparator #(.width(4), .mode("unsigned")) comparator_2 (
    .a(adder_2_out), .b(4'b1001), .gt(comparator_2_gt));  // open: eq, lt
  Comparator #(.width(4), .mode("unsigned")) comparator_3 (
    .a(adder_3_out), .b(4'b1001), .gt(comparator_3_gt));  // open: eq, lt
  Comparator #(.width(4), .mode("unsigned")) comparator_4 (
    .a(adder_4_out), .b(4'b1001), .gt(comparator_4_gt));  // open: eq, lt
  Comparator #(.width(4), .mode("unsigned")) comparator_5 (
    .a(adder_5_out), .b(4'b1001), .gt(comparator_5_gt));  // open: eq, lt
  Comparator #(.width(4), .mode("unsigned")) comparator_6 (
    .a(adder_6_out), .b(4'b1001), .gt(comparator_6_gt));  // open: eq, lt
  Multiplexer #(.width(4), .enable("false")) multiplexer_7 (
    .in0(4'b0000), .in1(4'b0110), .out(multiplexer_7_out), .sel(or_7_out));
  or or_7 (or_7_out, comparator_1_gt, adder_1_cout);
  or or_8 (or_8_out, comparator_2_gt, adder_2_cout);
  or or_9 (or_9_out, comparator_3_gt, adder_3_cout);
  or or_10 (or_10_out, comparator_4_gt, adder_4_cout);
  or or_11 (or_11_out, comparator_5_gt, adder_5_cout);
  or or_12 (or_12_out, comparator_6_gt, adder_6_cout);
  Multiplexer #(.width(4), .enable("false")) multiplexer_8 (
    .in0(4'b0000), .in1(4'b0110), .out(multiplexer_8_out), .sel(or_8_out));
  Multiplexer #(.width(4), .enable("false")) multiplexer_9 (
    .in0(4'b0000), .in1(4'b0110), .out(multiplexer_9_out), .sel(or_9_out));
  Multiplexer #(.width(4), .enable("false")) multiplexer_10 (
    .in0(4'b0000), .in1(4'b0110), .out(multiplexer_10_out), .sel(or_10_out));
  Multiplexer #(.width(4), .enable("false")) multiplexer_11 (
    .in0(4'b0000), .in1(4'b0110), .out(multiplexer_11_out), .sel(or_11_out));
  Multiplexer #(.width(4), .enable("false")) multiplexer_12 (
    .in0(4'b0000), .in1(4'b0110), .out(multiplexer_12_out), .sel(or_12_out));
  Adder #(.width(4)) adder_7 (
    .a(adder_1_out), .b(multiplexer_7_out), .out(adder_7_out), .cout(adder_7_cout));  // open: cin
  assign bit_extender_1_out = {{1{1'b0}}, Customer_1_number_of_days_selection};  // Bit_Extender bit_extender_1
  Adder #(.width(4)) adder_8 (
    .a(adder_2_out), .b(multiplexer_8_out), .out(adder_8_out), .cout(adder_8_cout));  // open: cin
  Adder #(.width(4)) adder_9 (
    .a(adder_3_out), .b(multiplexer_9_out), .out(adder_9_out), .cout(adder_9_cout));  // open: cin
  Adder #(.width(4)) adder_10 (
    .a(adder_4_out), .b(multiplexer_10_out), .out(adder_10_out), .cout(adder_10_cout));  // open: cin
  Adder #(.width(4)) adder_11 (
    .a(adder_5_out), .b(multiplexer_11_out), .out(adder_11_out), .cout(adder_11_cout));  // open: cin
  Adder #(.width(4)) adder_12 (
    .a(adder_6_out), .b(multiplexer_12_out), .out(adder_12_out), .cout(adder_12_cout));  // open: cin
  assign bit_extender_2_out = {{3{1'b0}}, or_3_out};  // Bit_Extender bit_extender_2
  assign bit_extender_3_out = {{1{1'b0}}, Customer_2_number_of_days_selection};  // Bit_Extender bit_extender_3
  assign bit_extender_4_out = {{3{1'b0}}, or_6_out};  // Bit_Extender bit_extender_4
  Multiplier #(.width(4)) multiplier_1 (
    .a(adder_7_out), .b(bit_extender_1_out), .out(multiplier_1_out), .cout(multiplier_1_cout));  // open: cin
  Multiplier #(.width(4)) multiplier_2 (
    .a(bit_extender_1_out), .b(adder_8_out), .out(multiplier_2_out), .cout(multiplier_2_cout));  // open: cin
  Multiplier #(.width(4)) multiplier_3 (
    .a(bit_extender_1_out), .b(adder_9_out), .out(multiplier_3_out), .cout(multiplier_3_cout));  // open: cin
  Multiplier #(.width(4)) multiplier_4 (
    .a(bit_extender_1_out), .b(bit_extender_2_out), .out(multiplier_4_out), .cout(multiplier_4_cout));  // open: cin
  Multiplier #(.width(4)) multiplier_5 (
    .a(adder_10_out), .b(bit_extender_3_out), .out(multiplier_5_out), .cout(multiplier_5_cout));  // open: cin
  Multiplier #(.width(4)) multiplier_6 (
    .a(bit_extender_3_out), .b(adder_11_out), .out(multiplier_6_out), .cout(multiplier_6_cout));  // open: cin
  Multiplier #(.width(4)) multiplier_7 (
    .a(bit_extender_3_out), .b(adder_12_out), .out(multiplier_7_out), .cout(multiplier_7_cout));  // open: cin
  Multiplier #(.width(4)) multiplier_8 (
    .a(bit_extender_3_out), .b(bit_extender_4_out), .out(multiplier_8_out), .cout(multiplier_8_cout));  // open: cin
  assign bit_extender_5_out = {{3{1'b0}}, multiplier_1_out};  // Bit_Extender bit_extender_5
  assign bit_extender_6_out = {{3{1'b0}}, multiplier_1_cout};  // Bit_Extender bit_extender_6
  assign bit_extender_7_out = {{3{1'b0}}, multiplier_2_out};  // Bit_Extender bit_extender_7
  assign bit_extender_8_out = {{3{1'b0}}, multiplier_2_cout};  // Bit_Extender bit_extender_8
  assign bit_extender_9_out = {{3{1'b0}}, multiplier_3_out};  // Bit_Extender bit_extender_9
  assign bit_extender_10_out = {{3{1'b0}}, multiplier_3_cout};  // Bit_Extender bit_extender_10
  assign bit_extender_11_out = {{3{1'b0}}, multiplier_4_out};  // Bit_Extender bit_extender_11
  assign bit_extender_12_out = {{3{1'b0}}, multiplier_4_cout};  // Bit_Extender bit_extender_12
  assign bit_extender_13_out = {{3{1'b0}}, multiplier_5_out};  // Bit_Extender bit_extender_13
  assign bit_extender_14_out = {{3{1'b0}}, multiplier_5_cout};  // Bit_Extender bit_extender_14
  assign bit_extender_15_out = {{3{1'b0}}, multiplier_6_out};  // Bit_Extender bit_extender_15
  assign bit_extender_16_out = {{3{1'b0}}, multiplier_6_cout};  // Bit_Extender bit_extender_16
  assign bit_extender_17_out = {{3{1'b0}}, multiplier_7_out};  // Bit_Extender bit_extender_17
  assign bit_extender_18_out = {{3{1'b0}}, multiplier_7_cout};  // Bit_Extender bit_extender_18
  assign bit_extender_19_out = {{3{1'b0}}, multiplier_8_out};  // Bit_Extender bit_extender_19
  assign bit_extender_20_out = {{3{1'b0}}, multiplier_8_cout};  // Bit_Extender bit_extender_20
  Shifter #(.width(7)) shifter_1 (.in(bit_extender_6_out), .\dist (3'b100), .out(shifter_1_out));
  Shifter #(.width(7)) shifter_2 (.in(bit_extender_8_out), .\dist (3'b100), .out(shifter_2_out));
  Shifter #(.width(7)) shifter_3 (.in(bit_extender_10_out), .\dist (3'b100), .out(shifter_3_out));
  Shifter #(.width(7)) shifter_4 (.in(bit_extender_12_out), .\dist (3'b100), .out(shifter_4_out));
  Shifter #(.width(7)) shifter_5 (.in(bit_extender_14_out), .\dist (3'b100), .out(shifter_5_out));
  Shifter #(.width(7)) shifter_6 (.in(bit_extender_16_out), .\dist (3'b100), .out(shifter_6_out));
  Shifter #(.width(7)) shifter_7 (.in(bit_extender_18_out), .\dist (3'b100), .out(shifter_7_out));
  Shifter #(.width(7)) shifter_8 (.in(bit_extender_20_out), .\dist (3'b100), .out(shifter_8_out));
  Adder #(.width(7)) adder_13 (.a(bit_extender_5_out), .b(shifter_1_out), .out(adder_13_out));  // open: cin, cout
  Adder #(.width(7)) adder_14 (.a(bit_extender_7_out), .b(shifter_2_out), .out(adder_14_out));  // open: cin, cout
  Adder #(.width(7)) adder_15 (.a(bit_extender_9_out), .b(shifter_3_out), .out(adder_15_out));  // open: cin, cout
  Adder #(.width(7)) adder_16 (
    .a(bit_extender_11_out), .b(shifter_4_out), .out(adder_16_out), .cout(adder_16_cout));  // open: cin
  Adder #(.width(7)) adder_17 (.a(bit_extender_13_out), .b(shifter_5_out), .out(adder_17_out));  // open: cin, cout
  Adder #(.width(7)) adder_18 (.a(bit_extender_15_out), .b(shifter_6_out), .out(adder_18_out));  // open: cin, cout
  Adder #(.width(7)) adder_19 (.a(bit_extender_17_out), .b(shifter_7_out), .out(adder_19_out));  // open: cin, cout
  Adder #(.width(7)) adder_20 (
    .a(bit_extender_19_out), .b(shifter_8_out), .out(adder_20_out), .cout(adder_20_cout));  // open: cin
  _7_bit_binary_to_BCD_converter u_7_bit_binary_to_bcd_converter_1 (
    .Output_LSB(n7_bit_binary_to_bcd_converter_1_output_lsb),
    .Output_MSB(n7_bit_binary_to_bcd_converter_1_output_msb), ._7_bit_binary_input(adder_13_out));
  _7_bit_binary_to_BCD_converter u_7_bit_binary_to_bcd_converter_2 (
    .Output_LSB(n7_bit_binary_to_bcd_converter_2_output_lsb),
    .Output_MSB(n7_bit_binary_to_bcd_converter_2_output_msb), ._7_bit_binary_input(adder_14_out));
  _7_bit_binary_to_BCD_converter u_7_bit_binary_to_bcd_converter_3 (
    .Output_LSB(n7_bit_binary_to_bcd_converter_3_output_lsb),
    .Output_MSB(n7_bit_binary_to_bcd_converter_3_output_msb), ._7_bit_binary_input(adder_15_out));
  _7_bit_binary_to_BCD_converter u_7_bit_binary_to_bcd_converter_4 (
    .Output_LSB(n7_bit_binary_to_bcd_converter_4_output_lsb),
    .Output_MSB(n7_bit_binary_to_bcd_converter_4_output_msb), ._7_bit_binary_input(adder_16_out));
  assign bit_extender_21_out = {{3{1'b0}}, adder_16_cout};  // Bit_Extender bit_extender_21
  _7_bit_binary_to_BCD_converter u_7_bit_binary_to_bcd_converter_5 (
    .Output_LSB(n7_bit_binary_to_bcd_converter_5_output_lsb),
    .Output_MSB(n7_bit_binary_to_bcd_converter_5_output_msb), ._7_bit_binary_input(adder_17_out));
  _7_bit_binary_to_BCD_converter u_7_bit_binary_to_bcd_converter_6 (
    .Output_LSB(n7_bit_binary_to_bcd_converter_6_output_lsb),
    .Output_MSB(n7_bit_binary_to_bcd_converter_6_output_msb), ._7_bit_binary_input(adder_18_out));
  _7_bit_binary_to_BCD_converter u_7_bit_binary_to_bcd_converter_7 (
    .Output_LSB(n7_bit_binary_to_bcd_converter_7_output_lsb),
    .Output_MSB(n7_bit_binary_to_bcd_converter_7_output_msb), ._7_bit_binary_input(adder_19_out));
  _7_bit_binary_to_BCD_converter u_7_bit_binary_to_bcd_converter_8 (
    .Output_LSB(n7_bit_binary_to_bcd_converter_8_output_lsb),
    .Output_MSB(n7_bit_binary_to_bcd_converter_8_output_msb), ._7_bit_binary_input(adder_20_out));
  assign bit_extender_22_out = {{3{1'b0}}, adder_20_cout};  // Bit_Extender bit_extender_22
  or or_13 (or_13_out, adder_21_cout, adder_31_cout);
  or or_14 (or_14_out, adder_22_cout, adder_33_cout);
  or or_15 (or_15_out, adder_23_cout, adder_34_cout);
  or or_16 (or_16_out, adder_24_cout, adder_35_cout);
  Adder #(.width(4)) adder_21 (
    .a(n7_bit_binary_to_bcd_converter_1_output_lsb), .b(4'b0000), .out(adder_21_out), .cout(adder_21_cout));  // open: cin
  Adder #(.width(4)) adder_22 (
    .a(n7_bit_binary_to_bcd_converter_1_output_msb), .b(n7_bit_binary_to_bcd_converter_2_output_lsb),
    .out(adder_22_out), .cin(or_13_out), .cout(adder_22_cout));
  Adder #(.width(4)) adder_23 (
    .a(n7_bit_binary_to_bcd_converter_2_output_msb), .b(n7_bit_binary_to_bcd_converter_3_output_lsb),
    .out(adder_23_out), .cin(or_14_out), .cout(adder_23_cout));
  Adder #(.width(4)) adder_24 (
    .a(n7_bit_binary_to_bcd_converter_3_output_msb), .b(n7_bit_binary_to_bcd_converter_4_output_lsb),
    .out(adder_24_out), .cin(or_15_out), .cout(adder_24_cout));
  Adder #(.width(4)) adder_25 (
    .a(n7_bit_binary_to_bcd_converter_4_output_msb), .b(bit_extender_21_out), .out(adder_25_out),
    .cin(or_16_out), .cout(adder_25_cout));
  Adder #(.width(4)) adder_26 (
    .a(n7_bit_binary_to_bcd_converter_5_output_lsb), .b(4'b0000), .out(adder_26_out), .cout(adder_26_cout));  // open: cin
  or or_17 (or_17_out, adder_26_cout, adder_36_cout);
  Adder #(.width(4)) adder_27 (
    .a(n7_bit_binary_to_bcd_converter_5_output_msb), .b(n7_bit_binary_to_bcd_converter_6_output_lsb),
    .out(adder_27_out), .cin(or_17_out), .cout(adder_27_cout));
  or or_18 (or_18_out, adder_27_cout, adder_37_cout);
  Adder #(.width(4)) adder_28 (
    .a(n7_bit_binary_to_bcd_converter_6_output_msb), .b(n7_bit_binary_to_bcd_converter_7_output_lsb),
    .out(adder_28_out), .cin(or_18_out), .cout(adder_28_cout));
  or or_19 (or_19_out, adder_28_cout, adder_38_cout);
  Adder #(.width(4)) adder_29 (
    .a(n7_bit_binary_to_bcd_converter_7_output_msb), .b(n7_bit_binary_to_bcd_converter_8_output_lsb),
    .out(adder_29_out), .cin(or_19_out), .cout(adder_29_cout));
  or or_20 (or_20_out, adder_29_cout, adder_39_cout);
  Adder #(.width(4)) adder_30 (
    .a(n7_bit_binary_to_bcd_converter_8_output_msb), .b(bit_extender_22_out), .out(adder_30_out),
    .cin(or_20_out), .cout(adder_30_cout));
  Comparator #(.width(4), .mode("unsigned")) comparator_7 (
    .a(adder_21_out), .b(4'b1001), .gt(comparator_7_gt));  // open: eq, lt
  Comparator #(.width(4), .mode("unsigned")) comparator_8 (
    .a(adder_22_out), .b(4'b1001), .gt(comparator_8_gt));  // open: eq, lt
  Comparator #(.width(4), .mode("unsigned")) comparator_9 (
    .a(adder_23_out), .b(4'b1001), .gt(comparator_9_gt));  // open: eq, lt
  Comparator #(.width(4), .mode("unsigned")) comparator_10 (
    .a(adder_24_out), .b(4'b1001), .gt(comparator_10_gt));  // open: eq, lt
  Comparator #(.width(4), .mode("unsigned")) comparator_11 (
    .a(adder_25_out), .b(4'b1001), .gt(comparator_11_gt));  // open: eq, lt
  Comparator #(.width(4), .mode("unsigned")) comparator_12 (
    .a(adder_30_out), .b(4'b1001), .gt(comparator_12_gt));  // open: eq, lt
  or or_21 (or_21_out, comparator_7_gt, adder_21_cout);
  Comparator #(.width(4), .mode("unsigned")) comparator_13 (
    .a(adder_26_out), .b(4'b1001), .gt(comparator_13_gt));  // open: eq, lt
  Comparator #(.width(4), .mode("unsigned")) comparator_14 (
    .a(adder_27_out), .b(4'b1001), .gt(comparator_14_gt));  // open: eq, lt
  Comparator #(.width(4), .mode("unsigned")) comparator_15 (
    .a(adder_28_out), .b(4'b1001), .gt(comparator_15_gt));  // open: eq, lt
  Comparator #(.width(4), .mode("unsigned")) comparator_16 (
    .a(adder_29_out), .b(4'b1001), .gt(comparator_16_gt));  // open: eq, lt
  Multiplexer #(.width(4), .enable("false")) multiplexer_13 (
    .in0(4'b0000), .in1(4'b0110), .out(multiplexer_13_out), .sel(or_21_out));
  Multiplexer #(.width(4), .enable("false")) multiplexer_14 (
    .in0(4'b0000), .in1(4'b0110), .out(multiplexer_14_out), .sel(or_22_out));
  or or_22 (or_22_out, comparator_8_gt, adder_22_cout);
  Multiplexer #(.width(4), .enable("false")) multiplexer_15 (
    .in0(4'b0000), .in1(4'b0110), .out(multiplexer_15_out), .sel(or_23_out));
  or or_23 (or_23_out, comparator_9_gt, adder_23_cout);
  Multiplexer #(.width(4), .enable("false")) multiplexer_16 (
    .in0(4'b0000), .in1(4'b0110), .out(multiplexer_16_out), .sel(or_24_out));
  or or_24 (or_24_out, comparator_10_gt, adder_24_cout);
  Multiplexer #(.width(4), .enable("false")) multiplexer_17 (
    .in0(4'b0000), .in1(4'b0110), .out(multiplexer_17_out), .sel(or_25_out));
  or or_25 (or_25_out, comparator_11_gt, adder_25_cout);
  or or_26 (or_26_out, comparator_13_gt, adder_26_cout);
  or or_27 (or_27_out, comparator_14_gt, adder_27_cout);
  or or_28 (or_28_out, comparator_15_gt, adder_28_cout);
  or or_29 (or_29_out, comparator_16_gt, adder_29_cout);
  or or_30 (or_30_out, comparator_12_gt, adder_30_cout);
  Adder #(.width(4)) adder_31 (.a(adder_21_out), .b(multiplexer_13_out), .out(LSB), .cout(adder_31_cout));  // open: cin
  Adder #(.width(4)) adder_32 (.a(adder_25_out), .b(multiplexer_17_out), .out(MSB));  // open: cin, cout
  Multiplexer #(.width(4), .enable("false")) multiplexer_18 (
    .in0(4'b0000), .in1(4'b0110), .out(multiplexer_18_out), .sel(or_26_out));
  Multiplexer #(.width(4), .enable("false")) multiplexer_19 (
    .in0(4'b0000), .in1(4'b0110), .out(multiplexer_19_out), .sel(or_27_out));
  Multiplexer #(.width(4), .enable("false")) multiplexer_20 (
    .in0(4'b0000), .in1(4'b0110), .out(multiplexer_20_out), .sel(or_28_out));
  Multiplexer #(.width(4), .enable("false")) multiplexer_21 (
    .in0(4'b0000), .in1(4'b0110), .out(multiplexer_21_out), .sel(or_29_out));
  Multiplexer #(.width(4), .enable("false")) multiplexer_22 (
    .in0(4'b0000), .in1(4'b0110), .out(multiplexer_22_out), .sel(or_30_out));
  Adder #(.width(4)) adder_33 (
    .a(adder_22_out), .b(multiplexer_14_out), .out(out_6), .cout(adder_33_cout));  // open: cin
  Adder #(.width(4)) adder_34 (
    .a(adder_23_out), .b(multiplexer_15_out), .out(out_7), .cout(adder_34_cout));  // open: cin
  Adder #(.width(4)) adder_35 (
    .a(adder_24_out), .b(multiplexer_16_out), .out(out_8), .cout(adder_35_cout));  // open: cin
  Adder #(.width(4)) adder_36 (
    .a(adder_26_out), .b(multiplexer_18_out), .out(LSB_2), .cout(adder_36_cout));  // open: cin
  Adder #(.width(4)) adder_37 (
    .a(adder_27_out), .b(multiplexer_19_out), .out(out_11), .cout(adder_37_cout));  // open: cin
  Adder #(.width(4)) adder_38 (
    .a(adder_28_out), .b(multiplexer_20_out), .out(out_12), .cout(adder_38_cout));  // open: cin
  Adder #(.width(4)) adder_39 (
    .a(adder_29_out), .b(multiplexer_21_out), .out(out_13), .cout(adder_39_cout));  // open: cin
  Adder #(.width(4)) adder_40 (.a(adder_30_out), .b(multiplexer_22_out), .out(MSB_2));  // open: cin, cout

  // Notes on the sheet:
  //   Wi-Fi charges
  //   LSB
  //   MSB
  //   Room charges
  //   LSB
  //   MSB
  //   Wi-Fi+room charges adder
  //   Wi-Fi+room charges adder
  //   Multiply one day charges and number of days
  //   Multiply one day charges and number of days
  //   7 bit binary to BCD converter
  //   7 bit binary to BCD converter
  //   7 bit binary to BCD converter
  //   7 bit binary to BCD converter
  //   7 bit binary to BCD converter
  //   7 bit binary to BCD converter
  //   7 bit binary to BCD converter
  //   7 bit binary to BCD converter
  //   Convert into BCD
  //   Convert into BCD
  //   Customer-1 total bill
  //   Customer-2 total bill
endmodule

// Special room for physically challenged people
module pwd_special_room_module (
  input  [2:0] Number_of_days_selection,
  input  Button,
  input  AC_selection,
  input  Wi_Fi_selection,
  input  [3:0] ID_input,
  output [2:0] Number_of_days_counter,
  output [2:0] Number_of_days,
  output AC,
  output Wi_Fi,
  output [3:0] MSB,
  output [3:0] out_11,
  output [3:0] out_12,
  output [3:0] out_13,
  output [3:0] LSB,
  output [3:0] ID,
  output Indicator
);

  wire and_1_out, and_2_out, and_3_out, and_4_out, clock_1_out, comparator_1_eq, comparator_2_eq,
       comparator_3_eq, comparator_5_eq, nor_1_out, not_1_out, not_2_out, not_3_out;

  Comparator #(.width(3), .mode("unsigned")) comparator_1 (
    .a(3'b000), .b(Number_of_days_selection), .eq(comparator_1_eq));  // open: gt, lt
  and and_1 (and_1_out, nor_1_out, comparator_3_eq);
  Comparator #(.width(4), .mode("unsigned")) comparator_2 (
    .a(4'b0000), .b(ID_input), .eq(comparator_2_eq));  // open: gt, lt
  and and_2 (and_2_out, nor_1_out, Indicator);
  Register #(.width(3)) register_1 (
    .D(Number_of_days_selection), .en(and_1_out), .Q(Number_of_days), .clk(Button), .clr(and_4_out));
  Register #(.width(1)) register_2 (.D(AC_selection), .en(and_1_out), .Q(AC), .clk(Button), .clr(and_4_out));
  Register #(.width(1)) register_3 (.D(Wi_Fi_selection), .en(and_1_out), .Q(Wi_Fi), .clk(Button), .clr(and_4_out));
  Register #(.width(4)) register_4 (.D(ID_input), .en(and_2_out), .Q(ID), .clk(Button), .clr(and_4_out));
  Comparator #(.width(3), .mode("unsigned")) comparator_3 (
    .a(Number_of_days), .b(3'b000), .eq(comparator_3_eq));  // open: gt, lt
  not not_1 (not_1_out, comparator_3_eq);
  Clock #(.highDuration(4), .lowDuration(4)) clock_1 (.out(clock_1_out));
  Comparator #(.width(4), .mode("unsigned")) comparator_4 (.a(ID), .b(4'b0000), .eq(Indicator));  // open: gt, lt
  not not_2 (not_2_out, comparator_3_eq);
  not not_3 (not_3_out, comparator_3_eq);
  and and_3 (and_3_out, not_1_out, clock_1_out);
  Counter #(.width(3), .max('h7)) counter_1 (
    .count(not_3_out), .Q(Number_of_days_counter), .clk(and_3_out), .clr(and_4_out));  // open: load, D, carry
  Comparator #(.width(3), .mode("unsigned")) comparator_5 (
    .a(Number_of_days), .b(Number_of_days_counter), .eq(comparator_5_eq));  // open: gt, lt
  and and_4 (and_4_out, not_2_out, comparator_5_eq);
  nor nor_1 (nor_1_out, comparator_1_eq, comparator_2_eq);
  Bill_calculator_module_for_pwd_special_room Bill_calculator (
    .Number_of_days(Number_of_days), .AC_selection(AC), .Wi_Fi_selection(Wi_Fi), .LSB(LSB), .out_5(out_13),
    .out_6(out_12), .MSB(MSB), .out_7(out_11));

  // Notes on the sheet:
  //   Bill
endmodule

// VIP
module vip_room_module (
  input  [2:0] Number_of_days_selection,
  input  Button,
  input  AC_selection,
  input  Wi_Fi_selection,
  input  [3:0] ID_input,
  output [2:0] NUmber_of_days_counter,
  output [2:0] Number_of_days,
  output AC,
  output [3:0] MSB,
  output [3:0] out_10,
  output [3:0] out_11,
  output [3:0] out_12,
  output [3:0] LSB,
  output Wi_Fi,
  output [3:0] ID,
  output Indicator
);

  wire and_1_out, and_2_out, and_3_out, and_4_out, clock_1_out, comparator_1_eq, comparator_2_eq,
       comparator_3_eq, comparator_5_eq, nor_1_out, not_1_out, not_2_out, not_3_out;

  Comparator #(.width(3), .mode("unsigned")) comparator_1 (
    .a(3'b000), .b(Number_of_days_selection), .eq(comparator_1_eq));  // open: gt, lt
  and and_1 (and_1_out, nor_1_out, comparator_3_eq);
  Comparator #(.width(4), .mode("unsigned")) comparator_2 (
    .a(4'b0000), .b(ID_input), .eq(comparator_2_eq));  // open: gt, lt
  Register #(.width(3)) register_1 (
    .D(Number_of_days_selection), .en(and_1_out), .Q(Number_of_days), .clk(Button), .clr(and_4_out));
  and and_2 (and_2_out, nor_1_out, Indicator);
  Register #(.width(1)) register_2 (.D(AC_selection), .en(and_1_out), .Q(AC), .clk(Button), .clr(and_4_out));
  Register #(.width(1)) register_3 (.D(Wi_Fi_selection), .en(and_1_out), .Q(Wi_Fi), .clk(Button), .clr(and_4_out));
  Register #(.width(4)) register_4 (.D(ID_input), .en(and_2_out), .Q(ID), .clk(Button), .clr(and_4_out));
  Comparator #(.width(3), .mode("unsigned")) comparator_3 (
    .a(Number_of_days), .b(3'b000), .eq(comparator_3_eq));  // open: gt, lt
  not not_1 (not_1_out, comparator_3_eq);
  not not_2 (not_2_out, comparator_3_eq);
  Clock #(.highDuration(4), .lowDuration(4)) clock_1 (.out(clock_1_out));
  Comparator #(.width(4), .mode("unsigned")) comparator_4 (.a(ID), .b(4'b0000), .eq(Indicator));  // open: gt, lt
  not not_3 (not_3_out, comparator_3_eq);
  Counter #(.width(3), .max('h7)) counter_1 (
    .count(not_1_out), .Q(NUmber_of_days_counter), .clk(and_3_out), .clr(and_4_out));  // open: load, D, carry
  and and_3 (and_3_out, not_2_out, clock_1_out);
  Comparator #(.width(3), .mode("unsigned")) comparator_5 (
    .a(Number_of_days), .b(NUmber_of_days_counter), .eq(comparator_5_eq));  // open: gt, lt
  and and_4 (and_4_out, not_3_out, comparator_5_eq);
  nor nor_1 (nor_1_out, comparator_1_eq, comparator_2_eq);
  Bill_calculator_module_for_vip_room Bill_calculator (
    .Number_of_days(Number_of_days), .AC_selection(AC), .Wi_Fi_selection(Wi_Fi), .LSB(LSB), .out_5(out_12),
    .out_6(out_11), .out_7(out_10), .MSB(MSB));

  // Notes on the sheet:
  //   Bill
endmodule

// Double sharing AC room
module double_sharing_ac_room_module (
  input  [2:0] Number_of_days_selection,
  input  Button,
  input  Wi_Fi_selection,
  input  [3:0] ID_input,
  output [2:0] Customer_1_number_of_days_counter,
  output [2:0] Number_of_days_of_customer_1,
  output [2:0] Number_of_days_of_customer_2,
  output [2:0] Customer_2_number_of_days_counter,
  output Customer_1_Wi_Fi,
  output Customer_2_Wi_Fi,
  output [3:0] MSB,
  output [3:0] out_12,
  output [3:0] out_13,
  output [3:0] out_14,
  output [3:0] LSB,
  output [3:0] MSB_2,
  output [3:0] out_17,
  output [3:0] out_18,
  output [3:0] out_19,
  output [3:0] LSB_2,
  output [3:0] Customer_1_ID,
  output [3:0] Customer_2_ID,
  output Indicator
);

  wire and_1_out, and_2_out, and_3_out, and_5_out, and_6_out, and_7_out, and_8_out, and_9_out, clock_1_out,
       clock_2_out, comparator_1_eq, comparator_2_eq, comparator_3_eq, comparator_4_eq, comparator_5_eq,
       comparator_6_eq, comparator_7_eq, comparator_8_eq, comparator_9_eq, comparator_10_eq, nor_1_out,
       not_1_out, not_2_out, not_3_out, not_4_out, not_5_out, not_6_out, not_7_out, not_8_out, not_9_out;

  Comparator #(.width(3), .mode("unsigned")) comparator_1 (
    .a(3'b000), .b(Number_of_days_selection), .eq(comparator_1_eq));  // open: gt, lt
  and and_1 (and_1_out, comparator_4_eq, nor_1_out, not_1_out);
  and and_2 (and_2_out, nor_1_out, comparator_3_eq);
  Comparator #(.width(4), .mode("unsigned")) comparator_2 (
    .a(4'b0000), .b(ID_input), .eq(comparator_2_eq));  // open: gt, lt
  Register #(.width(3)) register_1 (
    .D(Number_of_days_selection), .en(and_2_out), .Q(Number_of_days_of_customer_1), .clk(Button),
    .clr(and_8_out));
  Register #(.width(3)) register_2 (
    .D(Number_of_days_selection), .en(and_1_out), .Q(Number_of_days_of_customer_2), .clk(Button),
    .clr(and_9_out));
  and and_3 (and_3_out, nor_1_out, comparator_7_eq);
  not not_1 (not_1_out, comparator_3_eq);
  Register #(.width(1)) register_3 (
    .D(Wi_Fi_selection), .en(and_2_out), .Q(Customer_1_Wi_Fi), .clk(Button), .clr(and_8_out));
  Register #(.width(1)) register_4 (
    .D(Wi_Fi_selection), .en(and_5_out), .Q(Customer_2_Wi_Fi), .clk(Button), .clr(and_9_out));
  Register #(.width(4)) register_5 (.D(ID_input), .en(and_3_out), .Q(Customer_1_ID), .clk(Button), .clr(and_8_out));
  Register #(.width(4)) register_6 (.D(ID_input), .en(and_5_out), .Q(Customer_2_ID), .clk(Button), .clr(and_9_out));
  Comparator #(.width(3), .mode("unsigned")) comparator_3 (
    .a(Number_of_days_of_customer_1), .b(3'b000), .eq(comparator_3_eq));  // open: gt, lt
  Comparator #(.width(3), .mode("unsigned")) comparator_4 (
    .a(Number_of_days_of_customer_2), .b(3'b000), .eq(comparator_4_eq));  // open: gt, lt
  // AND_Gate and_4 has open pins: in0=comparator_6_eq, in1=not_3_out, out=open
  not not_2 (not_2_out, comparator_4_eq);
  Clock #(.highDuration(4), .lowDuration(4)) clock_1 (.out(clock_1_out));
  Comparator #(.width(1), .mode("unsigned")) comparator_5 (
    .a(Customer_1_Wi_Fi), .b(1'b0), .eq(comparator_5_eq));  // open: gt, lt
  Comparator #(.width(1), .mode("unsigned")) comparator_6 (
    .a(1'b0), .b(Customer_2_Wi_Fi), .eq(comparator_6_eq));  // open: gt, lt
  not not_3 (not_3_out, comparator_5_eq);
  and and_5 (and_5_out, comparator_8_eq, nor_1_out, not_7_out);
  not not_4 (not_4_out, comparator_3_eq);
  not not_5 (not_5_out, comparator_3_eq);
  and and_6 (and_6_out, not_5_out, clock_2_out);
  Clock #(.highDuration(4), .lowDuration(4)) clock_2 (.out(clock_2_out));
  not not_6 (not_6_out, comparator_4_eq);
  and and_7 (and_7_out, not_2_out, clock_1_out);
  Comparator #(.width(4), .mode("unsigned")) comparator_7 (
    .a(Customer_1_ID), .b(4'b0000), .eq(comparator_7_eq));  // open: gt, lt
  Comparator #(.width(4), .mode("unsigned")) comparator_8 (
    .a(4'b0000), .b(Customer_2_ID), .eq(comparator_8_eq));  // open: gt, lt
  not not_7 (not_7_out, comparator_7_eq);
  not not_8 (not_8_out, comparator_3_eq);
  Counter #(.width(3), .max('h7)) counter_1 (
    .count(not_4_out), .Q(Customer_1_number_of_days_counter), .clk(and_6_out), .clr(and_8_out));  // open: load, D, carry
  not not_9 (not_9_out, comparator_4_eq);
  Counter #(.width(3), .max('h7)) counter_2 (
    .count(not_6_out), .Q(Customer_2_number_of_days_counter), .clk(and_7_out), .clr(and_9_out));  // open: load, D, carry
  or or_1 (Indicator, comparator_7_eq, comparator_8_eq);
  Comparator #(.width(3), .mode("unsigned")) comparator_9 (
    .a(Number_of_days_of_customer_1), .b(Customer_1_number_of_days_counter), .eq(comparator_9_eq));  // open: gt, lt
  Comparator #(.width(3), .mode("unsigned")) comparator_10 (
    .a(Number_of_days_of_customer_2), .b(Customer_2_number_of_days_counter), .eq(comparator_10_eq));  // open: gt, lt
  and and_8 (and_8_out, not_8_out, comparator_9_eq);
  and and_9 (and_9_out, not_9_out, comparator_10_eq);
  nor nor_1 (nor_1_out, comparator_1_eq, comparator_2_eq);
  Bill_calculator_module_for_double_sharing_ac_room Bill_calculator (
    .Customer_1_number_of_days_selection(Number_of_days_of_customer_1),
    .Customer_1_Wi_Fi_selection(Customer_1_Wi_Fi),
    .Customer_2_number_of_days_selection(Number_of_days_of_customer_2),
    .Customer_2_Wi_Fi_selection(Customer_2_Wi_Fi), .LSB(LSB), .out_6(out_14), .MSB(MSB), .LSB_2(LSB_2),
    .out_11(out_19), .out_12(out_18), .out_13(out_17), .MSB_2(MSB_2), .out_8(out_12), .out_7(out_13));

  // Notes on the sheet:
  //   Customer-2 bill
  //   Customer-1 bill
endmodule
// Double sharing non-AC room
module double_sharing_non_ac_room_module (
  input  [2:0] Number_of_days_selection,
  input  Button,
  input  Wi_Fi_selection,
  input  [3:0] ID_input,
  output [2:0] Customer_1_number_of_days_counter,
  output [2:0] Number_of_days_of_customer_1,
  output [2:0] Number_of_days_of_customer_2,
  output [2:0] Customer_2_number_of_days_counter,
  output [3:0] MSB,
  output [3:0] out_10,
  output [3:0] out_11,
  output [3:0] out_12,
  output [3:0] LSB,
  output Customer_1_Wi_Fi,
  output [3:0] MSB_2,
  output [3:0] out_16,
  output [3:0] out_17,
  output [3:0] out_18,
  output [3:0] LSB_2,
  output Customer_2_Wi_Fi,
  output [3:0] Customer_1_ID,
  output Indicator,
  output [3:0] Customer_2_ID
);

  wire and_1_out, and_2_out, and_3_out, and_5_out, and_6_out, and_7_out, and_8_out, and_9_out, clock_1_out,
       clock_2_out, comparator_1_eq, comparator_2_eq, comparator_3_eq, comparator_4_eq, comparator_5_eq,
       comparator_6_eq, comparator_7_eq, comparator_8_eq, comparator_9_eq, comparator_10_eq, nor_1_out,
       not_1_out, not_2_out, not_3_out, not_4_out, not_5_out, not_6_out, not_7_out, not_8_out, not_9_out;

  Comparator #(.width(3), .mode("unsigned")) comparator_1 (
    .a(3'b000), .b(Number_of_days_selection), .eq(comparator_1_eq));  // open: gt, lt
  and and_1 (and_1_out, comparator_4_eq, nor_1_out, not_1_out);
  and and_2 (and_2_out, nor_1_out, comparator_3_eq);
  Comparator #(.width(4), .mode("unsigned")) comparator_2 (
    .a(4'b0000), .b(ID_input), .eq(comparator_2_eq));  // open: gt, lt
  Register #(.width(3)) register_1 (
    .D(Number_of_days_selection), .en(and_2_out), .Q(Number_of_days_of_customer_1), .clk(Button),
    .clr(and_8_out));
  Register #(.width(3)) register_2 (
    .D(Number_of_days_selection), .en(and_1_out), .Q(Number_of_days_of_customer_2), .clk(Button),
    .clr(and_9_out));
  and and_3 (and_3_out, nor_1_out, comparator_7_eq);
  not not_1 (not_1_out, comparator_3_eq);
  Register #(.width(1)) register_3 (
    .D(Wi_Fi_selection), .en(and_2_out), .Q(Customer_1_Wi_Fi), .clk(Button), .clr(and_8_out));
  Register #(.width(1)) register_4 (
    .D(Wi_Fi_selection), .en(and_5_out), .Q(Customer_2_Wi_Fi), .clk(Button), .clr(and_9_out));
  Register #(.width(4)) register_5 (.D(ID_input), .en(and_3_out), .Q(Customer_1_ID), .clk(Button), .clr(and_8_out));
  Register #(.width(4)) register_6 (.D(ID_input), .en(and_5_out), .Q(Customer_2_ID), .clk(Button), .clr(and_9_out));
  Comparator #(.width(3), .mode("unsigned")) comparator_3 (
    .a(Number_of_days_of_customer_1), .b(3'b000), .eq(comparator_3_eq));  // open: gt, lt
  Comparator #(.width(3), .mode("unsigned")) comparator_4 (
    .a(Number_of_days_of_customer_2), .b(3'b000), .eq(comparator_4_eq));  // open: gt, lt
  // AND_Gate and_4 has open pins: in0=comparator_6_eq, in1=not_2_out, out=open
  not not_2 (not_2_out, comparator_5_eq);
  and and_5 (and_5_out, comparator_8_eq, nor_1_out, not_6_out);
  not not_3 (not_3_out, comparator_3_eq);
  Clock #(.highDuration(4), .lowDuration(4)) clock_1 (.out(clock_1_out));
  not not_4 (not_4_out, comparator_4_eq);
  not not_5 (not_5_out, comparator_4_eq);
  Clock #(.highDuration(4), .lowDuration(4)) clock_2 (.out(clock_2_out));
  Comparator #(.width(1), .mode("unsigned")) comparator_5 (
    .a(Customer_1_Wi_Fi), .b(1'b0), .eq(comparator_5_eq));  // open: gt, lt
  Comparator #(.width(1), .mode("unsigned")) comparator_6 (
    .a(1'b0), .b(Customer_2_Wi_Fi), .eq(comparator_6_eq));  // open: gt, lt
  not not_6 (not_6_out, comparator_7_eq);
  not not_7 (not_7_out, comparator_3_eq);
  not not_8 (not_8_out, comparator_3_eq);
  and and_6 (and_6_out, not_3_out, clock_1_out);
  not not_9 (not_9_out, comparator_4_eq);
  Counter #(.width(3), .max('h7)) counter_1 (
    .count(not_4_out), .Q(Customer_2_number_of_days_counter), .clk(and_7_out), .clr(and_9_out));  // open: load, D, carry
  and and_7 (and_7_out, not_5_out, clock_2_out);
  Comparator #(.width(4), .mode("unsigned")) comparator_7 (
    .a(Customer_1_ID), .b(4'b0000), .eq(comparator_7_eq));  // open: gt, lt
  Comparator #(.width(4), .mode("unsigned")) comparator_8 (
    .a(4'b0000), .b(Customer_2_ID), .eq(comparator_8_eq));  // open: gt, lt
  Counter #(.width(3), .max('h7)) counter_2 (
    .count(not_8_out), .Q(Customer_1_number_of_days_counter), .clk(and_6_out), .clr(and_8_out));  // open: load, D, carry
  or or_1 (Indicator, comparator_7_eq, comparator_8_eq);
  Comparator #(.width(3), .mode("unsigned")) comparator_9 (
    .a(Number_of_days_of_customer_1), .b(Customer_1_number_of_days_counter), .eq(comparator_9_eq));  // open: gt, lt
  Comparator #(.width(3), .mode("unsigned")) comparator_10 (
    .a(Number_of_days_of_customer_2), .b(Customer_2_number_of_days_counter), .eq(comparator_10_eq));  // open: gt, lt
  and and_8 (and_8_out, not_7_out, comparator_9_eq);
  and and_9 (and_9_out, not_9_out, comparator_10_eq);
  nor nor_1 (nor_1_out, comparator_1_eq, comparator_2_eq);
  Bill_calculator_module_for_double_sharing_non_ac_room Bill_calculator (
    .Customer_1_number_of_days_selection(Number_of_days_of_customer_1),
    .Customer_2_number_of_days_selection(Number_of_days_of_customer_2),
    .Customer_2_Wi_Fi_selection_2(Customer_2_Wi_Fi), .out_6(LSB), .out_7(out_11), .out_8(out_10), .MSB(MSB),
    .LSB_2(LSB_2), .out_11(out_18), .out_12(out_17), .out_13(out_16), .MSB_2(MSB_2),
    .Customer_2_Wi_Fi_selection(Customer_1_Wi_Fi), .LSB(out_12));

  // Notes on the sheet:
  //   Customer-2 bill
  //   Customer-1 bill
endmodule

module ID_generator (
  input  in_1,
  output [3:0] out_2
);

  wire [3:0] counter_1_q;

  Counter #(.width(4), .max('hf)) counter_1 (.count(1'b1), .Q(counter_1_q), .clk(in_1));  // open: load, D, carry, clr
  Adder #(.width(4)) adder_1 (.a(counter_1_q), .b(4'b0001), .out(out_2));  // open: cin, cout
endmodule

module \final  (
  input  [2:0] Number_of_days,
  input  AC,
  input  Wi_Fi,
  output [2:0] Number_of_days_of_stay,
  output [2:0] Number_of_days_of_stay_of_customer_1,
  output [3:0] MSB,
  output [3:0] out_7,
  output [3:0] out_8,
  output [3:0] out_9,
  output [3:0] LSB,
  output [2:0] Number_of__days_elapsed,
  output [2:0] Number_of__days_elapsed_2,
  output [3:0] Customer_ID,
  output [3:0] ID_of_customer_1,
  output AC_2,
  output Customer_1_Wi_Fi,
  output Wi_Fi_2,
  output [2:0] Number_of_days_of_stay_of_customer_2,
  output [3:0] MSB_2,
  output [3:0] out_20,
  output [3:0] Bill,
  output [3:0] out_22,
  output [3:0] LSB_2,
  output [2:0] Number_of__days_elapsed_3,
  output [3:0] ID_of_customer_2,
  output Customer_2_Wi_Fi,
  output [2:0] Number_of_days_of_stay_2,
  output [2:0] Number_of__days_elapsed_4,
  output [3:0] Customer_ID_2,
  output AC_3,
  output Wi_Fi_3,
  output [3:0] MSB_3,
  output [3:0] out_33,
  output [3:0] out_34,
  output [3:0] out_35,
  output [3:0] LSB_3,
  output [2:0] Number_of_days_of_stay_of_customer_1_2,
  output [2:0] Number_of__days_elapsed_5,
  output [3:0] MSB_4,
  output [3:0] out_40,
  output [3:0] Bill_2,
  output [3:0] out_42,
  output [3:0] LSB_4,
  output [3:0] MSB_5,
  output [3:0] out_45,
  output [3:0] Customer_1_bill,
  output [3:0] out_47,
  output [3:0] LSB_5,
  output [3:0] ID_of_customer_1_2,
  output Customer_1_Wi_Fi_2,
  output [2:0] Number_of_days_of_stay_3,
  output [2:0] Number_of__days_elapsed_6,
  output [3:0] Customer_ID_3,
  output AC_4,
  output [2:0] Number_of_days_of_stay_of_customer_2_2,
  output Wi_Fi_4,
  output [2:0] Number_of__days_elapsed_7,
  output [3:0] ID_of_customer_2_2,
  output Customer_2_Wi_Fi_2,
  output [3:0] MSB_6,
  output [3:0] out_61,
  output [3:0] out_62,
  output [3:0] out_63,
  output [3:0] LSB_6,
  output [3:0] MSB_7,
  output [3:0] out_66,
  output [3:0] out_67,
  output [3:0] out_68,
  output [3:0] LSB_7
);

  wire and_1_out, and_2_out, and_3_out, and_4_out, and_5_out, Button_2_out, Button_3_out, Button_4_out,
       Button_5_out, Button_out, double_sharing_ac_room_module_1_indicator,
       double_sharing_non_ac_room_module_1_indicator, or_1_out, pwd_special_room_module_1_indicator,
       vip_room_module_1_indicator, vip_room_module_2_indicator;
  wire [3:0] id_generator_1_out_2;

  ID_generator id_generator_1 (.out_2(id_generator_1_out_2), .in_1(or_1_out));
  or or_1 (or_1_out, and_1_out, and_2_out, and_3_out, and_4_out, and_5_out);
  and and_1 (and_1_out, double_sharing_non_ac_room_module_1_indicator, Button_5_out);
  and and_2 (and_2_out, double_sharing_ac_room_module_1_indicator, Button_4_out);
  and and_3 (and_3_out, vip_room_module_2_indicator, Button_3_out);
  and and_4 (and_4_out, vip_room_module_1_indicator, Button_2_out);
  and and_5 (and_5_out, pwd_special_room_module_1_indicator, Button_out);
  Button Button (.out(Button_out));
  Button Button_2 (.out(Button_2_out));
  Button Button_3 (.out(Button_3_out));
  LED led_1 (.in(pwd_special_room_module_1_indicator));
  pwd_special_room_module pwd_special_room_module_1 (
    .Number_of_days_selection(Number_of_days), .Button(Button_out), .AC_selection(AC),
    .Wi_Fi_selection(Wi_Fi), .ID_input(id_generator_1_out_2),
    .Number_of_days_counter(Number_of__days_elapsed), .Number_of_days(Number_of_days_of_stay), .AC(AC_2),
    .Wi_Fi(Wi_Fi_2), .ID(Customer_ID), .Indicator(pwd_special_room_module_1_indicator), .MSB(MSB_2),
    .out_11(out_20), .out_12(Bill), .out_13(out_22), .LSB(LSB_2));
  LED led_2 (.in(vip_room_module_1_indicator));
  vip_room_module vip_room_module_1 (
    .Number_of_days_selection(Number_of_days), .Button(Button_2_out), .AC_selection(AC),
    .Wi_Fi_selection(Wi_Fi), .ID_input(id_generator_1_out_2),
    .NUmber_of_days_counter(Number_of__days_elapsed_4), .Number_of_days(Number_of_days_of_stay_2), .AC(AC_3),
    .Wi_Fi(Wi_Fi_3), .ID(Customer_ID_2), .Indicator(vip_room_module_1_indicator), .MSB(MSB_4),
    .out_10(out_40), .out_11(Bill_2), .out_12(out_42), .LSB(LSB_4));
  LED led_3 (.in(vip_room_module_2_indicator));
  vip_room_module vip_room_module_2 (
    .Number_of_days_selection(Number_of_days), .Button(Button_3_out), .AC_selection(AC),
    .Wi_Fi_selection(Wi_Fi), .ID_input(id_generator_1_out_2),
    .NUmber_of_days_counter(Number_of__days_elapsed_6), .Number_of_days(Number_of_days_of_stay_3), .AC(AC_4),
    .Wi_Fi(Wi_Fi_4), .ID(Customer_ID_3), .Indicator(vip_room_module_2_indicator), .MSB(MSB_6),
    .out_10(out_61), .out_11(out_62), .out_12(out_63), .LSB(LSB_6));
  Button Button_4 (.out(Button_4_out));
  Button Button_5 (.out(Button_5_out));
  double_sharing_non_ac_room_module double_sharing_non_ac_room_module_1 (
    .Number_of_days_selection(Number_of_days), .Button(Button_5_out), .Wi_Fi_selection(Wi_Fi),
    .ID_input(id_generator_1_out_2), .Customer_1_number_of_days_counter(Number_of__days_elapsed_5),
    .Number_of_days_of_customer_1(Number_of_days_of_stay_of_customer_1_2),
    .Number_of_days_of_customer_2(Number_of_days_of_stay_of_customer_2_2),
    .Customer_2_number_of_days_counter(Number_of__days_elapsed_7), .Customer_1_Wi_Fi(Customer_1_Wi_Fi_2),
    .Customer_2_Wi_Fi(Customer_2_Wi_Fi_2), .Customer_1_ID(ID_of_customer_1_2),
    .Indicator(double_sharing_non_ac_room_module_1_indicator), .Customer_2_ID(ID_of_customer_2_2),
    .MSB_2(MSB_7), .out_16(out_66), .out_17(out_67), .out_18(out_68), .LSB_2(LSB_7), .MSB(MSB_5),
    .out_10(out_45), .out_11(Customer_1_bill), .out_12(out_47), .LSB(LSB_5));
  LED led_4 (.in(double_sharing_ac_room_module_1_indicator));
  double_sharing_ac_room_module double_sharing_ac_room_module_1 (
    .Number_of_days_selection(Number_of_days), .Button(Button_4_out), .Wi_Fi_selection(Wi_Fi),
    .ID_input(id_generator_1_out_2), .Customer_1_number_of_days_counter(Number_of__days_elapsed_2),
    .Number_of_days_of_customer_1(Number_of_days_of_stay_of_customer_1),
    .Number_of_days_of_customer_2(Number_of_days_of_stay_of_customer_2),
    .Customer_2_number_of_days_counter(Number_of__days_elapsed_3), .Customer_1_Wi_Fi(Customer_1_Wi_Fi),
    .Customer_1_ID(ID_of_customer_1), .Indicator(double_sharing_ac_room_module_1_indicator),
    .Customer_2_ID(ID_of_customer_2), .MSB_2(MSB_3), .out_17(out_33), .out_18(out_34), .out_19(out_35),
    .LSB_2(LSB_3), .MSB(MSB), .out_12(out_7), .out_13(out_8), .out_14(out_9), .LSB(LSB),
    .Customer_2_Wi_Fi(Customer_2_Wi_Fi));
  LED led_5 (.in(double_sharing_non_ac_room_module_1_indicator));

  // Notes on the sheet:
  //   One day charges for double sharing AC room = 600
  //   Unique ID generator
  //   Bills are calculated according to these prices
  //   One day Wi-Fi charges = 100
  //   One day AC charges = 200
  //   One day charges for pwd special room = 500 
  //   One day charges for VIP room = 700
  //   One day charges for double sharing non-AC room = 400
  //   Team details
  //   A. Karun Suhas 231CS210
  //   D. Kranthi Kiran 231CS219
  //   D. Sahil Arshan 231CS223
  //   Bill
  //   Main circuit
  //   2.Ensure that the clock ticks are enabled.
  //   9.The bill is displayed in BCD form upto 5 digits.
  //   13. The two double sharing rooms are indicated AC and non-AC rooms.
  //   4. Real time room availability is indicated by the red and green lights corresponding to the room.
  //   3. Customers input their required facilities, duration of stay and click a button corresponding to the room they desire.
  //   5. If there is a vacancy in a room, it is indicated by green light. If the room is fully occupied, it is indicated by red light
  //   7. The customer ID, the facilities opted and the bill are displayed in the corresponding room module of the chosen room.
  //   14. The process is very much the same for the double sharing rooms as well, but it works for two persons.
  //   INSTRUCTIONS
  //   1. The project is to design and implement a digital system to efficiently allocate hotel rooms, calculate bills, and minimize manual errors.
  //   6. The system generates a unique customer ID for each customer and calculates the bill when the allotment process is successful.
  //   10. "Number of days of stay" port in the output section of each room module is a register which stores the number of days input by the customer.
  //   12. When the "number of days elapsed" value equals the value of  "number of days of stay", the room module is cleared which indicates that the room is deallocated.
  //   8. The AC and WI-Fi ports in the output section are indicate their selection by the customer. 1 indicates that the particular facility is selected, 0 indicates that the particular facility is not selected.
  //   11. "Number of days elapsed" port in the output section of each room is a counter which activates counting when the room is occupied. It counts the number of days elapsed after occupying the room. (Clock ticks need to be enabled).
  //   Customer-2 bill
  //   Customer-2 bill
  //   Customer-1 bill
endmodule
